// Digital circuit ALU.dig as structural Verilog
module ALU (
  input  [7:0] A,
  input  [7:0] B,
  input  [3:0] S,
  input  CI,
  input  SOE,
  input  DLOE,
  input  DHOE,
  output [7:0] O,
  output CO
);

  wire not_1_out;

  not not_1 (not_1_out, SOE);
  ALUD alud_1 (.CI(CI), .A(A), .B(B), .S(S), .LOE(DLOE), .HOE(DHOE), .Q(O), .CO(CO));
  EEPROM #(.AddrBits(13), .isProgramMemory("true"), .Bits(8)) ALUS (
    .A({CI, S, A}), .CS(~1'b0), .WE(~1'b1), .OE(~not_1_out), .D(O));

  // Notes on the sheet:
  //   contents of ALUS (hex, n*v repeats v):
  //   0,1,2,3,4,5,6,7,40,41,42,43,44,45,46,47,10,11,12,13,14,15,16,17,50,51,52,53,54,55,
  //   56,57,20,21,22,23,24,25,26,27,60,61,62,63,64,65,66,67,30,31,32,33,34,35,36,37,70,
  //   71,72,73,74,75,76,77,8,9,a,b,c,d,e,f,48,49,4a,4b,4c,4d,4e,4f,18,19,1a,1b,1c,1d,1e,
  //   1f,58,59,5a,5b,5c,5d,5e,5f,28,29,2a,2b,2c,2d,2e,2f,68,69,6a,6b,6c,6d,6e,6f,38,39,
  //   3a,3b,3c,3d,3e,3f,78,79,7a,7b,7c,7d,7e,7f,80,81,82,83,84,85,86,87,c0,c1,c2,c3,c4,
  //   c5,c6,c7,90,91,92,93,94,95,96,97,d0,d1,d2,d3,d4,d5,d6,d7,a0,a1,a2,a3,a4,a5,a6,a7,
  //   e0,e1,e2,e3,e4,e5,e6,e7,b0,b1,b2,b3,b4,b5,b6,b7,f0,f1,f2,f3,f4,f5,f6,f7,88,89,8a,
  //   8b,8c,8d,8e,8f,c8,c9,ca,cb,cc,cd,ce,cf,98,99,9a,9b,9c,9d,9e,9f,d8,d9,da,db,dc,dd,
  //   de,df,a8,a9,aa,ab,ac,ad,ae,af,e8,e9,ea,eb,ec,ed,ee,ef,b8,b9,ba,bb,bc,bd,be,bf,f8,
  //   f9,fa,fb,fc,fd,fe,ff,3,b,13,1b,3,b,13,1b,3,b,13,1b,3,b,13,1b,3,b,13,1b,3,b,13,1b,
  //   3,b,13,1b,3,b,13,1b,3,b,13,1b,3,b,13,1b,3,b,13,1b,3,b,13,1b,3,b,13,1b,3,b,13,1b,3,
  //   b,13,1b,3,b,13,1b,3,b,13,1b,3,b,13,1b,3,b,13,1b,3,b,13,1b,3,b,13,1b,3,b,13,1b,3,b,
  //   13,1b,3,b,13,1b,3,b,13,1b,3,b,13,1b,3,b,13,1b,3,b,13,1b,3,b,13,1b,3,b,13,1b,3,b,13,
  //   1b,3,b,13,1b,3,b,13,1b,3,b,13,1b,3,b,13,1b,3,b,13,1b,3,b,13,1b,3,b,13,1b,3,b,13,1b,
  //   3,b,13,1b,3,b,13,1b,3,b,13,1b,3,b,13,1b,3,b,13,1b,3,b,13,1b,3,b,13,1b,3,b,13,1b,3,
  //   b,13,1b,3,b,13,1b,3,b,13,1b,3,b,13,1b,3,b,13,1b,3,b,13,1b,3,b,13,1b,3,b,13,1b,3,b,
  //   13,1b,3,b,13,1b,3,b,13,1b,3,b,13,1b,3,b,13,1b,3,b,13,1b,3,b,13,1b,3,b,13,1b,3,b,13,
  //   1b,0,0,0,0,0,0,0,0,0,0,0,0,0,0,0,0,0,0,0,0,0,0,0,0,0,0,0,0,0,0,0,0,0,0,0,0,0,0,0,
  //   0,0,0,0,0,0,0,0,0,0,0,0,0,0,0,0,0,0,0,0,0,0,0,0,0,0,0,0,0,0,0,0,0,0,0,0,0,0,0,0,0,
  //   0,0,0,0,0,0,0,0,0,0,0,0,0,0,0,0,0,0,0,0,0,0,0,0,0,0,0,0,0,0,0,0,0,0,0,0,0,0,0,0,0,
  //   0,0,0,0,0,0,0,0,0,0,0,0,0,0,0,0,0,0,0,0,0,0,0,0,0,0,0,0,0,0,0,0,0,0,0,0,0,0,0,0,0,
  //   0,0,0,0,0,0,0,0,0,0,0,0,0,0,0,0,0,0,0,0,0,0,0,0,0,0,0,0,0,0,0,0,0,0,0,0,0,0,0,0,0,
  //   0,0,0,0,0,0,0,0,0,0,0,0,0,0,0,0,0,0,0,0,0,0,0,0,0,0,0,0,0,0,0,0,0,0,0,0,0,0,0,0,0,
  //   0,0,0,0,0,0,0,0,0,0,0,0,0,0,0,0,0,0,0,0,0,0,0,0,0,0,0,0,0,0,0,0,0,0,0,0,0,0,0,0,0,
  //   0,0,0,0,0,0,0,0,0,0,0,0,0,0,0,0,0,0,0,0,0,0,0,0,0,0,0,0,0,0,0,0,0,0,0,0,0,0,0,0,0,
  //   0,0,0,0,0,0,0,0,0,0,0,0,0,0,0,0,0,0,0,0,0,0,0,0,0,0,0,0,0,0,0,0,0,0,0,0,0,0,0,0,0,
  //   0,0,0,0,0,0,0,0,0,0,0,0,0,0,0,0,0,0,10,11,12,0,0,0,0,0,0,0,0,0,0,0,0,0,0,0,0,0,0,
  //   0,0,0,0,0,0,0,0,0,0,0,0,0,0,0,0,0,0,13,0,0,0,0,0,0,0,0,0,0,0,0,0,0,0,14,0,0,0,0,0,
  //   0,0,0,0,0,0,0,0,0,0,0,0,0,0,0,0,0,0,15,0,0,0,0,0,0,0,0,0,0,0,0,0,0,0,16,0,0,0,0,0,
  //   0,0,0,0,0,0,0,0,0,0,17,0,0,0,0,0,0,0,0,0,0,0,0,0,0,0,0,80,1,81,2,82,3,83,4,84,5,85,
  //   6,86,7,87,8,88,9,89,a,8a,b,8b,c,8c,d,8d,e,8e,f,8f,10,90,11,91,12,92,13,93,14,94,15,
  //   95,16,96,17,97,18,98,19,99,1a,9a,1b,9b,1c,9c,1d,9d,1e,9e,1f,9f,20,a0,21,a1,22,a2,
  //   23,a3,24,a4,25,a5,26,a6,27,a7,28,a8,29,a9,2a,aa,2b,ab,2c,ac,2d,ad,2e,ae,2f,af,30,
  //   b0,31,b1,32,b2,33,b3,34,b4,35,b5,36,b6,37,b7,38,b8,39,b9,3a,ba,3b,bb,3c,bc,3d,bd,
  //   3e,be,3f,bf,40,c0,41,c1,42,c2,43,c3,44,c4,45,c5,46,c6,47,c7,48,c8,49,c9,4a,ca,4b,
  //   cb,4c,cc,4d,cd,4e,ce,4f,cf,50,d0,51,d1,52,d2,53,d3,54,d4,55,d5,56,d6,57,d7,58,d8,
  //   59,d9,5a,da,5b,db,5c,dc,5d,dd,5e,de,5f,df,60,e0,61,e1,62,e2,63,e3,64,e4,65,e5,66,
  //   e6,67,e7,68,e8,69,e9,6a,ea,6b,eb,6c,ec,6d,ed,6e,ee,6f,ef,70,f0,71,f1,72,f2,73,f3,
  //   74,f4,75,f5,76,f6,77,f7,78,f8,79,f9,7a,fa,7b,fb,7c,fc,7d,fd,7e,fe,7f,ff,0,2,4,6,8,
  //   a,c,e,10,12,14,16,18,1a,1c,1e,20,22,24,26,28,2a,2c,2e,30,32,34,36,38,3a,3c,3e,40,
  //   42,44,46,48,4a,4c,4e,50,52,54,56,58,5a,5c,5e,60,62,64,66,68,6a,6c,6e,70,72,74,76,
  //   78,7a,7c,7e,80,82,84,86,88,8a,8c,8e,90,92,94,96,98,9a,9c,9e,a0,a2,a4,a6,a8,aa,ac,
  //   ae,b0,b2,b4,b6,b8,ba,bc,be,c0,c2,c4,c6,c8,ca,cc,ce,d0,d2,d4,d6,d8,da,dc,de,e0,e2,
  //   e4,e6,e8,ea,ec,ee,f0,f2,f4,f6,f8,fa,fc,fe,1,3,5,7,9,b,d,f,11,13,15,17,19,1b,1d,1f,
  //   21,23,25,27,29,2b,2d,2f,31,33,35,37,39,3b,3d,3f,41,43,45,47,49,4b,4d,4f,51,53,55,
  //   57,59,5b,5d,5f,61,63,65,67,69,6b,6d,6f,71,73,75,77,79,7b,7d,7f,81,83,85,87,89,8b,
  //   8d,8f,91,93,95,97,99,9b,9d,9f,a1,a3,a5,a7,a9,ab,ad,af,b1,b3,b5,b7,b9,bb,bd,bf,c1,
  //   c3,c5,c7,c9,cb,cd,cf,d1,d3,d5,d7,d9,db,dd,df,e1,e3,e5,e7,e9,eb,ed,ef,f1,f3,f5,f7,
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endmodule
