// Digital circuit ALUD.dig as structural Verilog
module ALUD (
  input  CI,
  input  [7:0] A,
  input  [7:0] B,
  input  [3:0] S,
  input  nLOE,
  input  nHOE,
  output [7:0] Q,
  output CO
);

  wire [6:0] ALUDH_d;
  wire [7:0] ALUDL_d;

  EEPROM #(.AddrBits(13), .isProgramMemory("true"), .Bits(8)) ALUDL (
    .A({CI, S, B[3:0], A[3:0]}), .CS(~1'b0), .WE(~1'b1), .OE(~1'b0), .D(ALUDL_d));
  EEPROM #(.AddrBits(13), .isProgramMemory("true"), .Bits(8)) ALUDH (
    .A({ALUDL_d[7], S, B[7:4], A[7:4]}), .CS(~1'b0), .WE(~1'b1), .OE(~1'b0), .D({CO, ALUDH_d}));
  assign Q = ~nLOE ? {ALUDH_d[3:0], ALUDL_d[3:0]} : 8'bz;  // DriverInvSel driverinvsel_1
  assign Q = ~nHOE ? {CO, ALUDH_d[6:4], ALUDL_d[7:4]} : 8'bz;  // DriverInvSel driverinvsel_2

  // Notes on the sheet:
  //   contents of ALUDL (hex, n*v repeats v):
  //   0,1,2,3,4,5,6,7,8,9,a,b,c,d,e,f,1,0,3,2,5,4,7,6,9,8,b,a,d,c,f,e,2,3,0,1,6,7,4,5,a,
  //   b,8,9,e,f,c,d,3,2,1,0,7,6,5,4,b,a,9,8,f,e,d,c,4,5,6,7,0,1,2,3,c,d,e,f,8,9,a,b,5,4,
  //   7,6,1,0,3,2,d,c,f,e,9,8,b,a,6,7,4,5,2,3,0,1,e,f,c,d,a,b,8,9,7,6,5,4,3,2,1,0,f,e,d,
  //   c,b,a,9,8,8,9,a,b,c,d,e,f,0,1,2,3,4,5,6,7,9,8,b,a,d,c,f,e,1,0,3,2,5,4,7,6,a,b,8,9,
  //   e,f,c,d,2,3,0,1,6,7,4,5,b,a,9,8,f,e,d,c,3,2,1,0,7,6,5,4,c,d,e,f,8,9,a,b,4,5,6,7,0,
  //   1,2,3,d,c,f,e,9,8,b,a,5,4,7,6,1,0,3,2,e,f,c,d,a,b,8,9,6,7,4,5,2,3,0,1,f,e,d,c,b,a,
  //   9,8,7,6,5,4,3,2,1,0,0,1,2,3,4,5,6,7,8,9,80,81,82,83,84,85,0,1,2,3,4,5,6,7,8,9,80,
  //   81,82,83,84,85,0,1,2,3,4,5,6,7,8,9,80,81,82,83,84,85,0,1,2,3,4,5,6,7,8,9,80,81,82,
  //   83,84,85,0,1,2,3,4,5,6,7,8,9,80,81,82,83,84,85,0,1,2,3,4,5,6,7,8,9,80,81,82,83,84,
  //   85,0,1,2,3,4,5,6,7,8,9,80,81,82,83,84,85,0,1,2,3,4,5,6,7,8,9,80,81,82,83,84,85,6,
  //   7,48,49,4a,4b,4c,4d,e,f,80,81,82,83,84,85,6,7,48,49,4a,4b,4c,4d,e,f,80,81,82,83,84,
  //   85,6,7,48,49,4a,4b,4c,4d,e,f,80,81,82,83,84,85,6,7,48,49,4a,4b,4c,4d,e,f,80,81,82,
  //   83,84,85,6,7,48,49,4a,4b,4c,4d,e,f,80,81,82,83,84,85,6,7,48,49,4a,4b,4c,4d,e,f,80,
  //   81,82,83,84,85,6,7,48,49,4a,4b,4c,4d,e,f,80,81,82,83,84,85,6,7,48,49,4a,4b,4c,4d,
  //   e,f,80,81,82,83,84,85,0,1,2,3,4,5,6,7,8,9,a,b,c,d,e,f,1,2,3,4,5,6,7,48,9,a,b,c,d,
  //   e,f,80,2,3,4,5,6,7,48,49,a,b,c,d,e,f,80,81,3,4,5,6,7,48,49,4a,b,c,d,e,f,80,81,82,
  //   4,5,6,7,48,49,4a,4b,c,d,e,f,80,81,82,83,5,6,7,48,49,4a,4b,4c,d,e,f,80,81,82,83,84,
  //   6,7,48,49,4a,4b,4c,4d,e,f,80,81,82,83,84,85,7,48,49,4a,4b,4c,4d,4e,f,80,81,82,83,
  //   84,85,86,8,9,a,b,c,d,e,f,c0,c1,c2,c3,c4,c5,c6,c7,9,a,b,c,d,e,f,80,c1,c2,c3,c4,c5,
  //   c6,c7,88,a,b,c,d,e,f,80,81,c2,c3,c4,c5,c6,c7,88,89,b,c,d,e,f,80,81,82,c3,c4,c5,c6,
  //   c7,88,89,8a,c,d,e,f,80,81,82,83,c4,c5,c6,c7,88,89,8a,8b,d,e,f,80,81,82,83,84,c5,c6,
  //   c7,88,89,8a,8b,8c,e,f,80,81,82,83,84,85,c6,c7,88,89,8a,8b,8c,8d,f,80,81,82,83,84,
  //   85,86,c7,88,89,8a,8b,8c,8d,8e,0,1,2,3,4,5,6,7,8,9,a,b,c,d,e,f,8f,0,1,2,3,4,5,6,47,
  //   8,9,a,b,c,d,e,8e,8f,0,1,2,3,4,5,46,47,8,9,a,b,c,d,8d,8e,8f,0,1,2,3,4,45,46,47,8,9,
  //   a,b,c,8c,8d,8e,8f,0,1,2,3,44,45,46,47,8,9,a,b,8b,8c,8d,8e,8f,0,1,2,43,44,45,46,47,
  //   8,9,a,8a,8b,8c,8d,8e,8f,0,1,42,43,44,45,46,47,8,9,89,8a,8b,8c,8d,8e,8f,0,41,42,43,
  //   44,45,46,47,8,c8,c9,ca,cb,cc,cd,ce,cf,0,1,2,3,4,5,6,7,87,c8,c9,ca,cb,cc,cd,ce,8f,
  //   0,1,2,3,4,5,6,86,87,c8,c9,ca,cb,cc,cd,8e,8f,0,1,2,3,4,5,85,86,87,c8,c9,ca,cb,cc,8d,
  //   8e,8f,0,1,2,3,4,84,85,86,87,c8,c9,ca,cb,8c,8d,8e,8f,0,1,2,3,83,84,85,86,87,c8,c9,
  //   ca,8b,8c,8d,8e,8f,0,1,2,82,83,84,85,86,87,c8,c9,8a,8b,8c,8d,8e,8f,0,1,81,82,83,84,
  //   85,86,87,c8,89,8a,8b,8c,8d,8e,8f,0,0,81,82,3,84,5,6,87,88,9,a,8b,c,8d,8e,f,0,81,82,
  //   3,84,5,6,87,88,9,a,8b,c,8d,8e,f,0,81,82,3,84,5,6,87,88,9,a,8b,c,8d,8e,f,0,81,82,3,
  //   84,5,6,87,88,9,a,8b,c,8d,8e,f,0,81,82,3,84,5,6,87,88,9,a,8b,c,8d,8e,f,0,81,82,3,84,
  //   5,6,87,88,9,a,8b,c,8d,8e,f,0,81,82,3,84,5,6,87,88,9,a,8b,c,8d,8e,f,0,81,82,3,84,5,
  //   6,87,88,9,a,8b,c,8d,8e,f,0,81,82,3,84,5,6,87,88,9,a,8b,c,8d,8e,f,0,81,82,3,84,5,6,
  //   87,88,9,a,8b,c,8d,8e,f,0,81,82,3,84,5,6,87,88,9,a,8b,c,8d,8e,f,0,81,82,3,84,5,6,87,
  //   88,9,a,8b,c,8d,8e,f,0,81,82,3,84,5,6,87,88,9,a,8b,c,8d,8e,f,0,81,82,3,84,5,6,87,88,
  //   9,a,8b,c,8d,8e,f,0,81,82,3,84,5,6,87,88,9,a,8b,c,8d,8e,f,0,81,82,3,84,5,6,87,88,9,
  //   a,8b,c,8d,8e,f,80,0,0,0,0,0,0,0,0,0,0,0,0,0,0,0,81,1,1,1,1,1,1,1,1,1,1,1,1,1,1,1,
  //   82,2,2,2,2,2,2,2,2,2,2,2,2,2,2,2,83,3,3,3,3,3,3,3,3,3,3,3,3,3,3,3,84,4,4,4,4,4,4,
  //   4,4,4,4,4,4,4,4,4,85,5,5,5,5,5,5,5,5,5,5,5,5,5,5,5,86,6,6,6,6,6,6,6,6,6,6,6,6,6,6,
  //   6,87,7,7,7,7,7,7,7,7,7,7,7,7,7,7,7,88,8,8,8,8,8,8,8,8,8,8,8,8,8,8,8,89,9,9,9,9,9,
  //   9,9,9,9,9,9,9,9,9,9,8a,a,a,a,a,a,a,a,a,a,a,a,a,a,a,a,8b,b,b,b,b,b,b,b,b,b,b,b,b,b,
  //   b,b,8c,c,c,c,c,c,c,c,c,c,c,c,c,c,c,c,8d,d,d,d,d,d,d,d,d,d,d,d,d,d,d,d,8e,e,e,e,e,
  //   e,e,e,e,e,e,e,e,e,e,e,8f,f,f,f,f,f,f,f,f,f,f,f,f,f,f,f,0,0,0,0,0,0,0,0,0,0,0,0,0,
  //   0,0,0,0,1,1,1,1,1,1,1,1,1,1,1,1,1,1,1,2,0,2,2,2,2,2,2,2,2,2,2,2,2,2,2,2,1,3,3,3,3,
  //   3,3,3,3,3,3,3,3,3,3,4,4,0,4,4,4,4,4,4,4,4,4,4,4,4,4,4,5,1,5,5,5,5,5,5,5,5,5,5,5,5,
  //   5,6,4,2,6,6,6,6,6,6,6,6,6,6,6,6,6,6,5,3,7,7,7,7,7,7,7,7,7,7,7,7,7,8,8,8,0,8,8,8,8,
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  //   contents of ALUDH (hex, n*v repeats v):
  //   0,1,2,3,4,5,6,7,8,9,a,b,c,d,e,f,1,0,3,2,5,4,7,6,9,8,b,a,d,c,f,e,2,3,0,1,6,7,4,5,a,
  //   b,8,9,e,f,c,d,3,2,1,0,7,6,5,4,b,a,9,8,f,e,d,c,4,5,6,7,0,1,2,3,c,d,e,f,8,9,a,b,5,4,
  //   7,6,1,0,3,2,d,c,f,e,9,8,b,a,6,7,4,5,2,3,0,1,e,f,c,d,a,b,8,9,7,6,5,4,3,2,1,0,f,e,d,
  //   c,b,a,9,8,8,9,a,b,c,d,e,f,0,1,2,3,4,5,6,7,9,8,b,a,d,c,f,e,1,0,3,2,5,4,7,6,a,b,8,9,
  //   e,f,c,d,2,3,0,1,6,7,4,5,b,a,9,8,f,e,d,c,3,2,1,0,7,6,5,4,c,d,e,f,8,9,a,b,4,5,6,7,0,
  //   1,2,3,d,c,f,e,9,8,b,a,5,4,7,6,1,0,3,2,e,f,c,d,a,b,8,9,6,7,4,5,2,3,0,1,f,e,d,c,b,a,
  //   9,8,7,6,5,4,3,2,1,0,0,1,2,3,4,5,6,7,8,9,80,81,82,83,84,85,0,1,2,3,4,5,6,7,8,9,80,
  //   81,82,83,84,85,0,1,2,3,4,5,6,7,8,9,80,81,82,83,84,85,0,1,2,3,4,5,6,7,8,9,80,81,82,
  //   83,84,85,0,1,2,3,4,5,6,7,8,9,80,81,82,83,84,85,0,1,2,3,4,5,6,7,8,9,80,81,82,83,84,
  //   85,0,1,2,3,4,5,6,7,8,9,80,81,82,83,84,85,0,1,2,3,4,5,6,7,8,9,80,81,82,83,84,85,6,
  //   7,48,49,4a,4b,4c,4d,e,f,80,81,82,83,84,85,6,7,48,49,4a,4b,4c,4d,e,f,80,81,82,83,84,
  //   85,6,7,48,49,4a,4b,4c,4d,e,f,80,81,82,83,84,85,6,7,48,49,4a,4b,4c,4d,e,f,80,81,82,
  //   83,84,85,6,7,48,49,4a,4b,4c,4d,e,f,80,81,82,83,84,85,6,7,48,49,4a,4b,4c,4d,e,f,80,
  //   81,82,83,84,85,6,7,48,49,4a,4b,4c,4d,e,f,80,81,82,83,84,85,6,7,48,49,4a,4b,4c,4d,
  //   e,f,80,81,82,83,84,85,0,1,2,3,4,5,6,7,8,9,a,b,c,d,e,f,1,2,3,4,5,6,7,48,9,a,b,c,d,
  //   e,f,80,2,3,4,5,6,7,48,49,a,b,c,d,e,f,80,81,3,4,5,6,7,48,49,4a,b,c,d,e,f,80,81,82,
  //   4,5,6,7,48,49,4a,4b,c,d,e,f,80,81,82,83,5,6,7,48,49,4a,4b,4c,d,e,f,80,81,82,83,84,
  //   6,7,48,49,4a,4b,4c,4d,e,f,80,81,82,83,84,85,7,48,49,4a,4b,4c,4d,4e,f,80,81,82,83,
  //   84,85,86,8,9,a,b,c,d,e,f,c0,c1,c2,c3,c4,c5,c6,c7,9,a,b,c,d,e,f,80,c1,c2,c3,c4,c5,
  //   c6,c7,88,a,b,c,d,e,f,80,81,c2,c3,c4,c5,c6,c7,88,89,b,c,d,e,f,80,81,82,c3,c4,c5,c6,
  //   c7,88,89,8a,c,d,e,f,80,81,82,83,c4,c5,c6,c7,88,89,8a,8b,d,e,f,80,81,82,83,84,c5,c6,
  //   c7,88,89,8a,8b,8c,e,f,80,81,82,83,84,85,c6,c7,88,89,8a,8b,8c,8d,f,80,81,82,83,84,
  //   85,86,c7,88,89,8a,8b,8c,8d,8e,0,1,2,3,4,5,6,7,8,9,a,b,c,d,e,f,8f,0,1,2,3,4,5,6,47,
  //   8,9,a,b,c,d,e,8e,8f,0,1,2,3,4,5,46,47,8,9,a,b,c,d,8d,8e,8f,0,1,2,3,4,45,46,47,8,9,
  //   a,b,c,8c,8d,8e,8f,0,1,2,3,44,45,46,47,8,9,a,b,8b,8c,8d,8e,8f,0,1,2,43,44,45,46,47,
  //   8,9,a,8a,8b,8c,8d,8e,8f,0,1,42,43,44,45,46,47,8,9,89,8a,8b,8c,8d,8e,8f,0,41,42,43,
  //   44,45,46,47,8,c8,c9,ca,cb,cc,cd,ce,cf,0,1,2,3,4,5,6,7,87,c8,c9,ca,cb,cc,cd,ce,8f,
  //   0,1,2,3,4,5,6,86,87,c8,c9,ca,cb,cc,cd,8e,8f,0,1,2,3,4,5,85,86,87,c8,c9,ca,cb,cc,8d,
  //   8e,8f,0,1,2,3,4,84,85,86,87,c8,c9,ca,cb,8c,8d,8e,8f,0,1,2,3,83,84,85,86,87,c8,c9,
  //   ca,8b,8c,8d,8e,8f,0,1,2,82,83,84,85,86,87,c8,c9,8a,8b,8c,8d,8e,8f,0,1,81,82,83,84,
  //   85,86,87,c8,89,8a,8b,8c,8d,8e,8f,0,0,81,82,3,84,5,6,87,88,9,a,8b,c,8d,8e,f,0,81,82,
  //   3,84,5,6,87,88,9,a,8b,c,8d,8e,f,0,81,82,3,84,5,6,87,88,9,a,8b,c,8d,8e,f,0,81,82,3,
  //   84,5,6,87,88,9,a,8b,c,8d,8e,f,0,81,82,3,84,5,6,87,88,9,a,8b,c,8d,8e,f,0,81,82,3,84,
  //   5,6,87,88,9,a,8b,c,8d,8e,f,0,81,82,3,84,5,6,87,88,9,a,8b,c,8d,8e,f,0,81,82,3,84,5,
  //   6,87,88,9,a,8b,c,8d,8e,f,0,81,82,3,84,5,6,87,88,9,a,8b,c,8d,8e,f,0,81,82,3,84,5,6,
  //   87,88,9,a,8b,c,8d,8e,f,0,81,82,3,84,5,6,87,88,9,a,8b,c,8d,8e,f,0,81,82,3,84,5,6,87,
  //   88,9,a,8b,c,8d,8e,f,0,81,82,3,84,5,6,87,88,9,a,8b,c,8d,8e,f,0,81,82,3,84,5,6,87,88,
  //   9,a,8b,c,8d,8e,f,0,81,82,3,84,5,6,87,88,9,a,8b,c,8d,8e,f,0,81,82,3,84,5,6,87,88,9,
  //   a,8b,c,8d,8e,f,0,0,0,0,0,0,0,0,0,0,0,0,0,0,0,0,1,1,1,1,1,1,1,1,1,1,1,1,1,1,1,1,2,
  //   2,2,2,2,2,2,2,2,2,2,2,2,2,2,2,3,3,3,3,3,3,3,3,3,3,3,3,3,3,3,3,4,4,4,4,4,4,4,4,4,4,
  //   4,4,4,4,4,4,5,5,5,5,5,5,5,5,5,5,5,5,5,5,5,5,6,6,6,6,6,6,6,6,6,6,6,6,6,6,6,6,7,7,7,
  //   7,7,7,7,7,7,7,7,7,7,7,7,7,8,8,8,8,8,8,8,8,8,8,8,8,8,8,8,8,9,9,9,9,9,9,9,9,9,9,9,9,
  //   9,9,9,9,a,a,a,a,a,a,a,a,a,a,a,a,a,a,a,a,b,b,b,b,b,b,b,b,b,b,b,b,b,b,b,b,c,c,c,c,c,
  //   c,c,c,c,c,c,c,c,c,c,c,d,d,d,d,d,d,d,d,d,d,d,d,d,d,d,d,e,e,e,e,e,e,e,e,e,e,e,e,e,e,
  //   e,e,f,f,f,f,f,f,f,f,f,f,f,f,f,f,f,f,0,0,0,0,0,0,0,0,0,0,0,0,0,0,0,0,1,1,1,1,0,1,1,
  //   1,1,1,1,1,0,1,1,1,2,2,2,2,2,0,2,2,2,2,2,2,2,0,2,2,3,3,3,3,2,1,3,3,3,3,3,3,2,1,3,3,
  //   4,4,4,4,4,4,0,4,4,4,4,4,4,4,0,4,5,5,5,5,4,5,1,5,5,5,5,5,4,5,1,5,6,6,6,6,6,4,2,6,6,
  //   6,6,6,6,4,2,6,7,7,7,7,6,5,3,7,7,7,7,7,6,5,3,7,8,8,8,8,8,8,8,0,8,8,8,8,8,8,8,0,9,9,
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endmodule
