// Digital circuit BR.dig as structural Verilog
module BR (
  input  CLK,
  input  nCLR,
  input  [2:0] S,
  input  I4,
  input  I5,
  input  I7,
  input  I6,
  output Q
);

  wire d_ff_1_nq, multiplexer_1_out, multiplexer_2_out;

  Multiplexer #(.Selector_Bits(3)) multiplexer_1 (
    .sel(S), .in_0(Q), .in_1(d_ff_1_nq), .in_2(1'b0), .in_3(1'b1), .in_4(I4), .in_5(I5), .in_6(I6),
    .in_7(I7), .out(multiplexer_1_out));
  Multiplexer multiplexer_2 (.sel(nCLR), .in_0(1'b0), .in_1(multiplexer_1_out), .out(multiplexer_2_out));
  D_FF d_ff_1 (.D(multiplexer_2_out), .C(CLK), .Q(Q), .nQ(d_ff_1_nq));

  // Notes on the sheet:
  //   CLK: Clock
  //   nCLR: Sync clear
endmodule
