// Digital circuit BUS_TRAN.dig as structural Verilog
module BUS_TRAN (
  input  SFR_HIT,
  input  SSFR,
  input  RAM_WE,
  input  nRAM_OE,
  input  [7:0] ADDR,
  input  [7:0] BUS_A,
  input  [7:0] BUS_B
);

  wire and_1_out, nOE, not_1_out, or_1_out, or_2_out, or_3_out;

  not not_1 (not_1_out, SFR_HIT);
  or or_1 (or_1_out, RAM_WE, ~nRAM_OE);  // Or
  and and_1 (and_1_out, ADDR[7], SSFR);
  nand nand_1 (nOE, not_1_out, or_1_out, and_1_out);
  or or_2 (or_2_out, ~RAM_WE, nOE);  // Or
  or or_3 (or_3_out, RAM_WE, nOE);
  assign BUS_B = ~or_2_out ? BUS_A : 8'bz;  // DriverInvSel driverinvsel_1
  assign BUS_A = ~or_3_out ? BUS_B : 8'bz;  // DriverInvSel driverinvsel_2

  // Other names for the same wires on the sheet: AB_nBA = RAM_WE

  // Notes on the sheet:
  //   ADDR: default 128
endmodule
