// Digital circuit DCOUTER.dig as structural Verilog
module DCOUTER (
  input  CLK,
  input  nCLR,
  input  CNT,
  input  nLE,
  input  [11:0] D,
  output [11:0] Q
);

  wire not_1_out, or_1_out;
  wire [11:0] add_1_s, and_1_out, bitextender_1_out, multiplexer_1_out;

  BitExtender #(.inputBits(1), .outputBits(12), .generic("ouputBits := int(args.Bits);")) bitextender_1 (
    .in(nCLR), .out(bitextender_1_out));
  not not_1 (not_1_out, nLE);
  assign and_1_out = multiplexer_1_out & bitextender_1_out;  // And and_1, 12 bits wide
  or or_1 (or_1_out, CNT, not_1_out);
  Register #(.Bits(12), .generic("Bits := int(args.Bits);")) DPC (.D(and_1_out), .C(CLK), .en(or_1_out), .Q(Q));
  Add #(.Bits(12), .generic("Bits := int(args.Bits);")) add_1 (.a(12'h1), .b(Q), .c_i(1'b0), .s(add_1_s));  // open: c_o
  Multiplexer #(.Bits(12), .generic("Bits := int(args.Bits);")) multiplexer_1 (
    .sel(not_1_out), .in_0(add_1_s), .in_1(D), .out(multiplexer_1_out));

  // Notes on the sheet:
  //   CNT: Q = Q + 1, lower priority than LE
  //   nLE: load value from D
endmodule
