// Digital circuit INT.dig as structural Verilog
// PC external, for debug purpose, laod PC from RF to this register.
// select byte PCEL when RS is 8, select byte PCEH when RS is 9.
module INT (
  input  CLK,
  input  CLR,
  input  [7:0] A,
  input  [7:0] D,
  input  WE,
  input  OE,
  input  IRQOE,
  input  CII
);

  wire and_1_out, and_2_out, and_3_out, and_4_out, comparator_1_eq, comparator_2_eq;
  wire [3:0] TCON_irq;
  wire [4:4] or_1_out;
  wire [7:0] SCON_q, TCON_q;

  Comparator #(.Bits(8)) comparator_1 (.a(A), .b(8'h88), .eq(comparator_1_eq));  // open: gt, lt
  Comparator #(.Bits(8)) comparator_2 (.a(A), .b(8'h98), .eq(comparator_2_eq));  // open: gt, lt
  and and_1 (and_1_out, WE, comparator_1_eq);
  and and_2 (and_2_out, comparator_1_eq, OE);
  and and_3 (and_3_out, WE, comparator_2_eq);
  and and_4 (and_4_out, comparator_2_eq, OE);
  INT_TCON TCON (.D(D), .WE(and_1_out), .CII(CII), .CLK(CLK), .CLR(CLR), .IRQ(TCON_irq), .Q(TCON_q));
  reg__sync_clear #(.generic("Bits := 8;")) SCON (.D(D), .CLK(CLK), .CLR(CLR), .nLE(and_3_out), .Q(SCON_q));
  or or_1 (or_1_out[4], SCON_q[0], SCON_q[1]);
  assign D = and_2_out ? TCON_q : 8'bz;  // Driver driver_1
  assign D = and_4_out ? SCON_q : 8'bz;  // Driver driver_2
  assign D = IRQOE ? {3'b000, or_1_out[4], TCON_irq} : 8'bz;  // Driver driver_3
endmodule
