// Digital circuit PCE.dig as structural Verilog
// PC external, for debug purpose, laod PC from RF to this register.
// select byte PCEL when RS is 8, select byte PCEH when RS is 9.
module PCE (
  input  CLK,
  input  [7:0] D,
  input  [3:0] RS,
  input  WE,
  output [15:0] Q
);

  wire and_1_out, and_2_out, comparator_1_eq, comparator_2_eq;
  wire [7:0] multiplexer_1_out, multiplexer_2_out;

  Comparator #(.Bits(4)) comparator_1 (.a(RS), .b(4'b1000), .eq(comparator_1_eq));  // open: gt, lt
  Comparator #(.Bits(4)) comparator_2 (.a(RS), .b(4'b1001), .eq(comparator_2_eq));  // open: gt, lt
  and and_1 (and_1_out, WE, comparator_1_eq);
  Multiplexer #(.Bits(8)) multiplexer_1 (.sel(and_1_out), .in_0(Q[7:0]), .in_1(D), .out(multiplexer_1_out));
  Multiplexer #(.Bits(8)) multiplexer_2 (.sel(and_2_out), .in_0(Q[15:8]), .in_1(D), .out(multiplexer_2_out));
  and and_2 (and_2_out, WE, comparator_2_eq);
  Register #(.Bits(16)) PCER (.D({multiplexer_2_out, multiplexer_1_out}), .C(CLK), .en(1'b1), .Q(Q));

  // Notes on the sheet:
  //   RS: Address, PCL is 8, PCH is 9
  //   WE: write low nibble
endmodule
