// Digital circuit PER_INT_IO.dig as structural Verilog
// interrupt, IO:
// UART: SBUF, SCON
// external int: TCON
module PER_INT_IO (
  input  CLK,
  input  nRST,
  input  [7:0] A,
  input  [7:0] D,
  input  nWE,
  input  nOE,
  input  [7:0] nIRR_CLRB,
  input  nEINT0,
  input  nEINT1,
  output [7:0] IRR_Q
);

  wire and_1_out, and_2_out, d_ff_1_q, d_ff_2_nq, d_ff_3_q, d_ff_4_nq, IE0, IE1, IT0, IT1, not_1_out,
       not_2_out, sfr_ctl_1_nwe, sfr_ctl_2_nwe, sfr_ctl_3_nwe, sfr_ctl_4_nwe, sfr_ctl_5_noe, sfr_ctl_5_nwe,
       sfr_ctl_6_noe, sfr_ctl_6_nwe, sfr_ctl_7_noe, sfr_ctl_7_nwe, T0OV, T1OV, TR0, TR1;
  wire [1:0] sfr_sbuf_1_ri;
  wire [7:1] sfr_tcon_1_q;

  SFR_CTL sfr_ctl_1 (.nSFR_WE(nWE), .nSFR_OE(nOE), .A(A), .MADDR(8'h8a), .nWE(sfr_ctl_1_nwe));  // open: nOE
  SFR_CTL sfr_ctl_2 (.nSFR_WE(nWE), .nSFR_OE(nOE), .A(A), .MADDR(8'h8c), .nWE(sfr_ctl_2_nwe));  // open: nOE
  SFR_CTL sfr_ctl_3 (.nSFR_WE(nWE), .nSFR_OE(nOE), .A(A), .MADDR(8'h8b), .nWE(sfr_ctl_3_nwe));  // open: nOE
  SFR_CTL sfr_ctl_4 (.nSFR_WE(nWE), .nSFR_OE(nOE), .A(A), .MADDR(8'h8d), .nWE(sfr_ctl_4_nwe));  // open: nOE
  not not_1 (not_1_out, nEINT0);
  D_FF d_ff_1 (.D(not_1_out), .C(CLK), .Q(d_ff_1_q));  // open: nQ
  D_FF d_ff_2 (.D(d_ff_1_q), .C(CLK), .nQ(d_ff_2_nq));  // open: Q
  SFR_TIMMER sfr_timmer_1 (
    .CLK(CLK), .nRST(nRST), .D(D), .nWEL(sfr_ctl_1_nwe), .nWEH(sfr_ctl_2_nwe), .CNTEN(TR0), .OV(T0OV));
  SFR_TIMMER sfr_timmer_2 (
    .CLK(CLK), .nRST(nRST), .D(D), .nWEL(sfr_ctl_3_nwe), .nWEH(sfr_ctl_4_nwe), .CNTEN(TR1), .OV(T1OV));
  and and_1 (and_1_out, d_ff_1_q, d_ff_2_nq);
  Multiplexer multiplexer_1 (.sel(IT0), .in_0(d_ff_1_q), .in_1(and_1_out), .out(IE0));
  SFR_CTL sfr_ctl_5 (.nSFR_WE(nWE), .nSFR_OE(nOE), .A(A), .MADDR(8'h88), .nWE(sfr_ctl_5_nwe), .nOE(sfr_ctl_5_noe));
  SFR_CTL sfr_ctl_6 (.nSFR_WE(nWE), .nSFR_OE(nOE), .A(A), .MADDR(8'h98), .nWE(sfr_ctl_6_nwe), .nOE(sfr_ctl_6_noe));
  SFR_CTL sfr_ctl_7 (.nSFR_WE(nWE), .nSFR_OE(nOE), .A(A), .MADDR(8'h99), .nWE(sfr_ctl_7_nwe), .nOE(sfr_ctl_7_noe));
  not not_2 (not_2_out, nEINT1);
  D_FF d_ff_3 (.D(not_2_out), .C(CLK), .Q(d_ff_3_q));  // open: nQ
  D_FF d_ff_4 (.D(d_ff_3_q), .C(CLK), .nQ(d_ff_4_nq));  // open: Q
  SFR_TCON sfr_tcon_1 (
    .CLK(CLK), .nRST(nRST), .D(D), .nWE(sfr_ctl_5_nwe), .nOE(sfr_ctl_5_noe), .IRQ({T1OV, IE1, T0OV, IE0}),
    .nIRR_CB(nIRR_CLRB[3:0]),
    .Q({sfr_tcon_1_q[7], TR1, sfr_tcon_1_q[5], TR0, sfr_tcon_1_q[3], IT1, sfr_tcon_1_q[1], IT0}),
    .IRRQ(IRR_Q[3:0]));
  SFR_SCON sfr_scon_1 (
    .CLK(CLK), .nRST(nRST), .D(D), .nWE(sfr_ctl_6_nwe), .nOE(sfr_ctl_6_noe), .IRQ(sfr_sbuf_1_ri),
    .IRRQ(IRR_Q[4]));  // open: Q
  SFR_SBUF sfr_sbuf_1 (
    .CLK(CLK), .D(D), .nWE(sfr_ctl_7_nwe), .nOE(sfr_ctl_7_noe), .RI(sfr_sbuf_1_ri[0]), .TI(sfr_sbuf_1_ri[1]));
  and and_2 (and_2_out, d_ff_3_q, d_ff_4_nq);
  Multiplexer multiplexer_2 (.sel(IT1), .in_0(d_ff_3_q), .in_1(and_2_out), .out(IE1));

  assign IRR_Q[7:5] = 3'b000;

  // Other names for the same wires on the sheet: ADDR_SFR[7:0] = A; BUS_D[7:0] = D; nSFR_OE = nOE; nSFR_WE = nWE

  // Notes on the sheet:
  //   A: address input
  //   D: Data Bus
  //   nWE: write enable
  //   The SFR in the corresponding address will read the data from  the data bus.
  //   nOE: output enable.
  //   The SFR in the corresponding address will drive the data  bus.
endmodule
