// Digital circuit RAM.dig as structural Verilog
// stop ouput clock if input S  is high. if go is 1, clock will ouput normally.
module RAM (
  input  AC,
  input  [7:0] A,
  input  WE,
  input  nOE,
  input  Dt,
  output [7:0] O
);

  wire and_1_out, nand_1_out;

  and and_1 (and_1_out, A[7], Dt);
  nand nand_1 (nand_1_out, WE, AC);
  RAMSinglePortSel #(.AddrBits(8), .isProgramMemory("true"), .Bits(8)) RAM (
    .A(A), .CS(~and_1_out), .WE(~nand_1_out), .OE(~nOE), .D(O));

  // Notes on the sheet:
  //   AC: Asynchronous clock specially prepared for RAM
  //   A: address
  //   Dt: Direct address mode flag, it's will disable RAM when address is in
  //   0x80-0xFF.
endmodule
