// Digital circuit ROM.dig as structural Verilog
module ROM (
  input  [15:0] A,
  input  nOE,
  input  [7:0] IMMED,
  input  CLK,
  input  nPRRWE,
  input  [7:0] D
);

  wire nA_B, nand_1_out, nBUFCE, nCE, not_1_out, nWE, or_1_out, or_2_out;
  wire [2:2] PRR_q;
  wire [7:0] PRTESTROM_d;

  Register #(.Bits(3)) PRR (.D(IMMED[2:0]), .C(CLK), .en(~nPRRWE), .Q({PRR_q[2], nCE, nA_B}));
  nand nand_1 (nand_1_out, nA_B, nA_B);
  not not_1 (not_1_out, nOE);
  ROM #(.AddrBits(16), .isProgramMemory("true"), .Bits(8)) ROM (.A(A), .sel(not_1_out), .D(D));
  and and_1 (nBUFCE, nOE, nand_1_out);
  xor xor_1 (nWE, PRR_q[2], 1'b1);
  RAMSinglePortSel #(.AddrBits(16), .Bits(8)) PRTESTROM (.A(A), .CS(~nCE), .WE(~nWE), .OE(~nA_B), .D(PRTESTROM_d));
  or or_1 (or_1_out, nBUFCE, ~nA_B);  // Or
  or or_2 (or_2_out, nBUFCE, nA_B);
  assign PRTESTROM_d = ~or_1_out ? D : 8'bz;  // DriverInvSel driverinvsel_1

  // Notes on the sheet:
  //   A: address
  //   nOE: default 1
  //   nPRRWE: default 1
  //   contents of ROM (hex, n*v repeats v):
  //   2,f,ba,2,0,6,b2,9,32,32,0,2,11,1b,0,0,0,0,0,2,10,93,0,0,0,0,0,2,0,9,2,3,2f,e8,64,
  //   80,f8,e9,33,e8,33,60,11,4,60,f0,ed,33,ec,33,70,9,e8,fc,e9,fd,ea,fe,eb,ff,22,4,60,
  //   de,d3,eb,9f,ea,9e,e9,9d,e8,c2,e7,8c,f0,c2,f7,95,f0,40,c,e8,cc,f8,e9,cd,f9,ea,ce,fa,
  //   eb,cf,fb,12,2,fa,85,d0,f0,58,4,70,3,20,d5,b3,e8,4,70,7,50,2,b2,d5,2,3,39,92,d5,ec,
  //   4,60,f7,e4,cc,c0,e0,c3,98,f8,60,3b,94,18,60,8,40,d,d0,e0,fb,2,3,11,e4,fb,fa,c9,fc,
  //   80,28,e8,30,e4,6,e4,c9,fb,e4,ca,fc,e8,30,e3,5,e4,c9,ca,cb,fc,e8,54,7,60,10,f8,c3,
  //   e9,13,f9,ea,13,fa,eb,13,fb,ec,13,fc,d8,f1,30,f5,2f,c3,e4,9c,fc,ef,9b,ff,ee,9a,fe,
  //   ed,99,fd,d0,e0,fb,ef,4e,4d,4c,70,12,22,db,3,2,3,36,ec,2c,fc,ef,33,ff,ee,33,fe,ed,
  //   33,fd,ed,30,e7,eb,2,3,11,ef,2b,ff,ee,3a,fe,ed,39,fd,d0,e0,fb,50,13,b,bb,0,3,2,3,39,
  //   ed,13,fd,ee,13,fe,ef,13,ff,ec,13,fc,2,3,11,ec,4d,60,11,e8,49,70,17,ed,33,ec,33,4,
  //   60,d,e4,fc,ff,fe,fd,22,e9,33,e8,33,4,70,f8,2,3,2f,12,2,fa,58,4,60,9,e4,cc,24,81,50,
  //   6,28,50,9,2,3,39,28,40,3,2,3,36,c0,e0,eb,4a,70,44,b9,80,6,d0,e0,fb,2,3,25,ef,4e,70,
  //   1c,bd,80,8,eb,ff,ea,fe,e9,fd,80,eb,e9,8d,f0,a4,fe,e5,f0,2,1,ff,e9,cd,f9,ea,fe,eb,
  //   ff,ef,89,f0,a4,fc,e5,f0,ce,89,f0,a4,2e,ff,e4,35,f0,cd,89,f0,a4,2d,fe,e4,35,f0,80,
  //   67,ef,4e,70,5,bd,80,d7,80,c3,ef,8b,f0,a4,ac,f0,ee,8b,f0,a4,2c,fc,e4,35,f0,f8,ef,8a,
  //   f0,a4,2c,e5,f0,38,fc,e4,33,cb,8d,f0,a4,2c,fc,e5,f0,3b,f8,ee,8a,f0,a4,2c,fc,e5,f0,
  //   38,f8,e4,33,cf,89,f0,a4,2c,fc,e5,f0,38,cf,34,0,ce,89,f0,a4,2f,ff,e5,f0,3e,fe,e4,33,
  //   c9,8d,f0,a4,2e,fe,e5,f0,39,cd,8a,f0,a4,2f,ff,e5,f0,3e,fe,e4,3d,fd,33,d0,e0,fb,50,
  //   7,b,bb,0,f,2,3,39,ec,2c,fc,ef,33,ff,ee,33,fe,ed,33,fd,2,3,11,2,3,39,ec,5d,4,60,5,
  //   e8,59,4,70,3,2,3,2f,12,2,fa,58,4,60,f6,ec,48,60,f2,ec,70,4,fd,fe,ff,22,c8,60,db,24,
  //   81,c8,50,9,c3,98,60,2,50,6,2,3,36,98,50,ca,f5,82,e9,29,4b,4a,70,5,ab,82,2,3,25,75,
  //   f0,0,7c,1a,78,80,c3,ef,9b,ee,9a,ed,99,40,d,c3,ef,9b,ff,ee,9a,fe,ed,99,fd,e8,42,f0,
  //   dc,23,ac,f0,d0,e0,ff,d0,e0,fe,d0,e0,fd,ab,82,20,e7,10,1b,eb,60,ba,ec,2c,fc,ef,33,
  //   ff,ee,33,fe,ed,33,fd,2,3,11,e8,3,f8,30,e7,5,c0,f0,75,f0,0,ef,2f,ff,ee,33,fe,ed,33,
  //   fd,40,b8,30,e7,c2,80,aa,75,f0,20,80,e,75,f0,10,80,5,75,f0,8,7d,0,7e,0,7f,0,33,92,
  //   d5,30,d5,3,12,6,81,ec,33,40,10,ef,33,ff,ee,33,fe,ed,33,fd,ec,33,fc,d5,f0,ed,22,e5,
  //   f0,24,7e,a2,d5,13,cc,92,e7,cd,ce,ff,22,e9,d2,e7,c9,33,e8,33,f8,92,d5,ed,d2,e7,cd,
  //   33,ec,33,fc,50,2,b2,d5,22,ec,30,e7,10,f,bf,0,c,e,be,0,8,d,bd,0,4,b,eb,60,14,a2,d5,
  //   eb,13,fc,ed,92,e7,fd,22,74,ff,fc,fd,fe,ff,22,e4,80,f8,a2,d5,74,ff,13,fc,7d,80,e4,
  //   80,ef,f9,20,e7,28,24,f9,50,3,79,7,e4,f4,24,2,fb,18,db,fd,e6,24,fb,50,14,e9,60,d,e4,
  //   f6,18,e6,4,f6,b4,a,8,e4,f6,d9,f5,74,1,f6,a,22,c2,d5,22,ed,33,ec,33,92,d5,fa,60,2a,
  //   b4,ff,33,ed,c2,e7,7b,ff,60,6,7a,3,79,98,e4,22,7a,3,79,a1,20,d5,4,7a,3,79,9c,22,4e,
  //   61,4e,0,2b,49,4e,46,0,2d,49,4e,46,0,e4,7a,8,f6,8,da,fc,7b,0,74,7,22,e8,c0,e0,ec,c0,
  //   e0,ed,c0,e0,ee,c0,e0,ef,c0,e0,ea,75,f0,10,a4,ca,ab,f0,75,f0,4d,a4,2b,fb,e4,35,f0,
  //   fc,ea,24,10,fa,eb,34,c5,fb,ec,34,d9,fc,ed,c2,e7,ff,75,f0,56,a4,f4,24,11,c5,f0,f4,
  //   34,c5,8f,f0,a4,2a,e5,f0,3b,e4,3c,f6,20,e7,14,12,4,a6,d0,e0,ff,d0,e0,fe,d0,e0,fd,d0,
  //   e0,fc,12,2,1f,80,14,f4,4,12,4,a6,d0,e0,ff,d0,e0,fe,d0,e0,fd,d0,e0,fc,12,1,16,d0,e0,
  //   f8,e6,fa,ed,d2,e7,cd,33,ec,33,24,82,fb,e4,c3,cf,33,cf,ce,33,ce,cd,33,cd,33,db,f3,
  //   7b,7,75,f0,a,84,60,4,f6,8,1b,a,e5,f0,f6,8,8f,f0,74,a,a4,ff,ac,f0,8e,f0,74,a,a4,2c,
  //   fe,ac,f0,50,1,c,8d,f0,74,a,a4,2c,fd,e4,35,f0,f6,8,db,de,74,7,22,3f,80,0,0,41,20,0,
  //   0,42,c8,0,0,44,7a,0,0,46,1c,40,0,47,c3,50,0,49,74,24,0,4b,18,96,80,4c,be,bc,20,5a,
  //   e,1b,ca,67,53,c2,1c,74,9d,c5,ae,fb,60,6,54,7,60,1c,23,23,12,4,d4,eb,54,38,60,9,12,
  //   4,c0,12,4,cf,12,1,16,ec,f8,ed,f9,ee,fa,ef,cb,22,eb,12,4,cf,80,f1,54,38,3,24,1c,90,
  //   4,76,fe,93,fc,e,ee,93,fd,e,ee,93,e,ce,93,ff,22,c2,d5,30,f7,7,b2,d5,63,f0,ff,5,f0,
  //   30,e7,c,b2,d5,f4,4,84,63,f0,ff,5,f0,80,1,84,30,d5,2,f4,4,22,bb,1,6,89,82,8a,83,e0,
  //   22,50,2,e7,22,bb,fe,2,e3,22,89,82,8a,83,e4,93,22,bb,1,c,e5,82,29,f5,82,e5,83,3a,f5,
  //   83,e0,22,50,6,e9,25,82,f8,e6,22,bb,fe,6,e9,25,82,f8,e2,22,e5,82,29,f5,82,e5,83,3a,
  //   f5,83,e4,93,22,bb,1,6,89,82,8a,83,f0,22,50,2,f7,22,bb,fe,1,f3,22,ef,8d,f0,a4,a8,f0,
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endmodule
