// Digital circuit SFR_TCON.dig as structural Verilog
// PC external, for debug purpose, laod PC from RF to this register.
// select byte PCEL when RS is 8, select byte PCEH when RS is 9.
module SFR_TCON (
  input  CLK,
  input  nRST,
  input  [7:0] D,
  input  nWE,
  input  nOE,
  input  [3:0] IRQ,
  input  [3:0] nIRR_CB,
  output [7:0] Q,
  output [3:0] IRRQ
);

  \reg  #(.generic("Bits := 8;")) reg_1 (
    .D(D), .CLK(CLK), .nWE(nWE), .SETB({IRQ[3], 1'b0, IRQ[1], 1'b0, IRQ[2], 1'b0, IRQ[0], 1'b0}),
    .nCLRB({nIRR_CB[3], 1'b1, nIRR_CB[1], 1'b1, nIRR_CB[2], 1'b1, nIRR_CB[0], 1'b1}), .nRST(nRST),
    .Q({IRRQ[3], Q[6], IRRQ[1], Q[4], IRRQ[2], Q[2], IRRQ[0], Q[0]}));
  assign D = ~nOE ? {IRRQ[3], Q[6], IRRQ[1], Q[4], IRRQ[2], Q[2], IRRQ[0], Q[0]} : 8'bz;  // DriverInvSel driverinvsel_1

  assign {Q[7], Q[5], Q[3], Q[1]} = {IRRQ[3], IRRQ[1], IRRQ[2], IRRQ[0]};

  // Notes on the sheet:
  //   nRST: default 1
  //   nWE: default 1
  //   nOE: default 1
  //   nIRR_CB: default 15
  //   0-3: IE0,TF0,IE1,TF1
endmodule
