// Digital circuit SFR_TIMMER.dig as structural Verilog
// The timer component of hm51.
// It contains two registers named TL and TH,
// which form a 16-bit register T to store the reload value, 
// and a 16-bit counter to count and generate the OV flag.
module SFR_TIMMER (
  input  C,
  input  nR,
  input  [7:0] D,
  input  rld,
  input  nWEL,
  input  nWEH,
  input  en,
  output ovf,
  output [15:0] Q
);

  wire nor_1_out;
  wire [7:0] TH_q, TL_q;

  reg__sync_clear #(.generic("Bits := 8;")) TL (.D(D), .CLK(C), .CLR(nR), .LE(nWEL), .Q(TL_q));
  reg__sync_clear #(.generic("Bits := 8;")) TH (.D(D), .CLK(C), .CLR(nR), .LE(nWEH), .Q(TH_q));
  nor nor_1 (nor_1_out, ovf, rld);
  // Probe TIMMERL on {TH_q, TL_q}
  CounterPreset #(.Bits(16)) counterpreset_1 (
    .en(en), .C(C), .dir(1'b0), .in({TH_q, TL_q}), .ld(~nor_1_out), .clr(~nR), .out(Q), .ovf(ovf));

  // Other names for the same wires on the sheet: CLK = C; nRST = nR

  // Notes on the sheet:
  //   C: Hz: 800
  //   nR: reset, activated at 0, default 1
  //   D: data bus
  //   ovf: overflow flag of counter.
  //   rld: enable the counter to count, default 1
  //   nWEL: If it's 0, the value at 'D' is stored in the TL at the next clock signal., default 1
  //   nWEH: If it's 0, the value at 'D' is stored in the TH at the next clock signal., default 1
  //   Q: the value of counter.
  //   en: reload the value of counter from the register, default 1
endmodule
