// Digital circuit TOP.dig as structural Verilog
module TOP (
  input  CLK,
  input  [11:0] MIPCBI,
  input  MIPCBE,
  input  [15:0] PCBIA1,
  input  PCBE1,
  input  [15:0] PCBIA2,
  input  PCBE2,
  input  [31:0] in_10,
  output CLK_2,
  output [7:0] BUS_D,
  output [11:0] MIPC
);

  wire and_2_out, and_3_out, and_4_out, AST_FAIL, button_1_out, button_4_out, button_5_out, comparator_1_eq,
       comparator_2_eq, comparator_3_eq, core_1_p16, dipswitch_1_out, DUMP_p5, EXIT_p5, GENCLKBRK, IRQ, nCLR,
       nINT1, nIRR_CLR, nITN0, nSFR_OE, nSFR_WE, or_1_out, reset_1_out;
  wire [3:0] register_1_q, register_1_q_2, register_2_q, register_2_q_2, register_3_q, register_3_q_2,
       register_4_q, register_4_q_2, register_5_q, register_6_q, register_6_q_2, register_7_q,
       register_7_q_2, register_8_q, register_8_q_2;
  wire [7:0] ADDR_SFR, opcode_q, PORT0_q, PORT1_q;
  wire [7:4] register_5_q_2;
  wire [15:0] PC;
  wire [23:0] counter_1_out;
  wire [31:0] add_1_s, add_2_s, add_3_s, op_count_d, op_tick_total_d, op_tickcnt_out, tick_total;

  // ASSERT ASSERT: pin names not known; wires that end beside it: CLK_2, ADDR_SFR, BUS_D, nSFR_WE, AST_FAIL
  // EXTCTL EXIT: pin names not known; wires that end beside it: CLK_2, ADDR_SFR, BUS_D, nSFR_WE, EXIT_p5
  // DUMP DUMP: pin names not known; wires that end beside it: CLK_2, ADDR_SFR, BUS_D, nSFR_WE, DUMP_p5
  // PER_INT_IO per_int_io_1: pin names not known; wires that end beside it: CLK_2, nCLR, ADDR_SFR, BUS_D, nSFR_WE, nSFR_OE, nIRR_CLR, nITN0, nINT1, IRQ
  // Probe on EXIT_p5
  // Probe on DUMP_p5
  // Probe on IRQ
  // Probe on PC
  // Probe on MIPC
  SFR_GENERIC_REG #(.generic("Bits := 8;")) PORT1 (
    .CLK(CLK_2), .nRST(nCLR), .A(ADDR_SFR), .D(BUS_D), .SETB({8{1'b0}}), .nCLRB({8{1'b1}}),
    .nSFR_WE(nSFR_WE), .nSFR_OE(nSFR_OE), .MADDR(8'h90), .Q(PORT1_q));
  SFR_GENERIC_REG #(.generic("Bits := 8;")) PORT0 (
    .CLK(CLK_2), .nRST(nCLR), .A(ADDR_SFR), .D(BUS_D), .SETB({8{1'b0}}), .nCLRB({8{1'b1}}),
    .nSFR_WE(nSFR_WE), .nSFR_OE(nSFR_OE), .MADDR(8'h80), .Q(PORT0_q));
  Button #(.activeLow("true")) button_1 (.out(button_1_out));
  Button #(.activeLow("true")) button_2 (.out(nITN0));
  Button #(.activeLow("true")) button_3 (.out(nINT1));
  Comparator #(.Bits(12)) comparator_1 (.a(MIPCBI), .b(MIPC), .eq(comparator_1_eq));  // open: gt, lt
  Comparator #(.Bits(16)) comparator_2 (.a(PCBIA1), .b(PC), .eq(comparator_2_eq));  // open: gt, lt
  Comparator #(.Bits(16)) comparator_3 (.a(PCBIA2), .b(PC), .eq(comparator_3_eq));  // open: gt, lt
  Reset reset_1 (.out(reset_1_out));
  and and_1 (nCLR, reset_1_out, button_1_out);
  and and_2 (and_2_out, comparator_1_eq, MIPCBE);
  and and_3 (and_3_out, comparator_2_eq, PCBE1);
  and and_4 (and_4_out, comparator_3_eq, PCBE2);
  Seven_Seg #(.ledPersistence("true"), .commonConnectionType("anode")) seven_seg_1 (
    .a(register_1_q[0]), .b(register_1_q[1]), .c(register_1_q[2]), .d(register_1_q[3]),
    .e(register_1_q_2[0]), .f(register_1_q_2[1]), .g(register_1_q_2[2]), .dp(register_1_q_2[3]));
  DipSwitch dipswitch_1 (.out(dipswitch_1_out));
  Register #(.Bits(8)) register_1 (.D(PORT1_q), .C(PORT0_q[7]), .en(1'b1), .Q({register_1_q_2, register_1_q}));
  Button button_4 (.out(button_4_out));
  Button button_5 (.out(button_5_out));
  or or_1 (or_1_out, and_2_out, and_3_out, and_4_out, AST_FAIL, GENCLKBRK);
  Seven_Seg #(.ledPersistence("true"), .commonConnectionType("anode")) seven_seg_2 (
    .a(register_2_q[0]), .b(register_2_q[1]), .c(register_2_q[2]), .d(register_2_q[3]),
    .e(register_2_q_2[0]), .f(register_2_q_2[1]), .g(register_2_q_2[2]), .dp(register_2_q_2[3]));
  // CORE core_1: pin names not known; wires that end beside it: CLK, nCLR, IRQ, button_4_out, dipswitch_1_out, button_5_out, or_1_out, PC, MIPC, CLK_2, BUS_D, ADDR_SFR, nSFR_WE, nSFR_OE, nIRR_CLR, core_1_p16
  Register #(.Bits(8)) register_2 (.D(PORT1_q), .C(PORT0_q[6]), .en(1'b1), .Q({register_2_q_2, register_2_q}));
  Counter #(.Bits(32)) tickcnt (.en(~or_1_out), .C(CLK_2), .clr(~nCLR), .out(tick_total));  // open: ovf
  Comparator #(.Bits(32)) comparator_4 (.a(tick_total), .b(in_10), .eq(GENCLKBRK));  // open: gt, lt
  Seven_Seg #(.ledPersistence("true"), .commonConnectionType("anode")) seven_seg_3 (
    .a(register_3_q[0]), .b(register_3_q[1]), .c(register_3_q[2]), .d(register_3_q[3]),
    .e(register_3_q_2[0]), .f(register_3_q_2[1]), .g(register_3_q_2[2]), .dp(register_3_q_2[3]));
  Register #(.Bits(8)) register_3 (.D(PORT1_q), .C(PORT0_q[5]), .en(1'b1), .Q({register_3_q_2, register_3_q}));
  // Probe tick_total on tick_total
  Seven_Seg #(.ledPersistence("true"), .commonConnectionType("anode")) seven_seg_4 (
    .a(register_4_q[0]), .b(register_4_q[1]), .c(register_4_q[2]), .d(register_4_q[3]),
    .e(register_4_q_2[0]), .f(register_4_q_2[1]), .g(register_4_q_2[2]), .dp(register_4_q_2[3]));
  Register #(.Bits(8)) register_4 (.D(PORT1_q), .C(PORT0_q[4]), .en(1'b1), .Q({register_4_q_2, register_4_q}));
  Seven_Seg #(.ledPersistence("true"), .commonConnectionType("anode")) seven_seg_5 (
    .a(register_5_q[0]), .b(register_5_q[1]), .c(register_5_q[2]), .d(register_5_q[3]),
    .e(register_5_q_2[4]), .f(register_5_q_2[5]), .g(register_5_q_2[6]), .dp(register_5_q_2[7]));
  // Probe on BUS_D
  Register #(.Bits(8)) opcode (.D(BUS_D), .C(CLK_2), .en(core_1_p16), .Q(opcode_q));
  Counter #(.Bits(32)) op_tickcnt (.en(1'b1), .C(CLK_2), .clr(core_1_p16), .out(op_tickcnt_out));  // open: ovf
  Register #(.Bits(8)) register_5 (.D(PORT1_q), .C(PORT0_q[3]), .en(1'b1), .Q({register_5_q_2, register_5_q}));
  // Probe on op_tickcnt_out
  Seven_Seg #(.ledPersistence("true"), .commonConnectionType("anode")) seven_seg_6 (
    .a(register_6_q[0]), .b(register_6_q[1]), .c(register_6_q[2]), .d(register_6_q[3]),
    .e(register_6_q_2[0]), .f(register_6_q_2[1]), .g(register_6_q_2[2]), .dp(register_6_q_2[3]));
  Counter #(.Bits(24)) counter_1 (.en(core_1_p16), .C(CLK_2), .clr(~nCLR), .out(counter_1_out));  // open: ovf
  Add #(.Bits(32)) add_1 (.a(op_tickcnt_out), .b(32'h1), .c_i(1'b0), .s(add_1_s));  // open: c_o
  Register #(.Bits(8)) register_6 (.D(PORT1_q), .C(PORT0_q[2]), .en(1'b1), .Q({register_6_q_2, register_6_q}));
  Add #(.Bits(32)) add_2 (.a(add_1_s), .b(op_tick_total_d), .c_i(1'b0), .s(add_2_s));  // open: c_o
  Seven_Seg #(.ledPersistence("true"), .commonConnectionType("anode")) seven_seg_7 (
    .a(register_7_q[0]), .b(register_7_q[1]), .c(register_7_q[2]), .d(register_7_q[3]),
    .e(register_7_q_2[0]), .f(register_7_q_2[1]), .g(register_7_q_2[2]), .dp(register_7_q_2[3]));
  RAMDualPort #(.AddrBits(24), .Bits(16)) PCtrace (
    .A(counter_1_out), .Din(PC), .str(core_1_p16), .C(CLK_2), .ld(1'b1));  // open: D
  RAMDualPort #(.AddrBits(8), .Bits(32)) op_count (
    .A(BUS_D), .Din(add_3_s), .str(core_1_p16), .C(CLK_2), .ld(1'b1), .D(op_count_d));
  Register #(.Bits(8)) register_7 (.D(PORT1_q), .C(PORT0_q[1]), .en(1'b1), .Q({register_7_q_2, register_7_q}));
  // Probe on opcode_q
  Seven_Seg #(.ledPersistence("true"), .commonConnectionType("anode")) seven_seg_8 (
    .a(register_8_q[0]), .b(register_8_q[1]), .c(register_8_q[2]), .d(register_8_q[3]),
    .e(register_8_q_2[0]), .f(register_8_q_2[1]), .g(register_8_q_2[2]), .dp(register_8_q_2[3]));
  Add #(.Bits(32)) add_3 (.a(32'h1), .b(op_count_d), .c_i(1'b0), .s(add_3_s));  // open: c_o
  RAMDualPort #(.AddrBits(8), .Bits(32)) op_tick_total (
    .A(opcode_q), .Din(add_2_s), .str(core_1_p16), .C(CLK_2), .ld(1'b1), .D(op_tick_total_d));
  RAMDualPort #(.AddrBits(8), .Bits(32)) op_tick_aver (
    .A(opcode_q), .Din(add_1_s), .str(core_1_p16), .C(CLK_2), .ld(1'b1));  // open: D
  Register #(.Bits(8)) register_8 (.D(PORT1_q), .C(PORT0_q[0]), .en(1'b1), .Q({register_8_q_2, register_8_q}));

  // Other names for the same wires on the sheet: CLK_t = CLK_2

  // Notes on the sheet:
  //   CLK: Hz: 2147483647
  //   MIPCBI: default 521
  //   PCBIA1: default 1407
  //   in_10: default 4294967295
  //   contents of ROM (hex, n*v repeats v):
  //   2,24,f5,2,28,6,e4,f5,f,22,0,2,24,17,0,0,0,0,0,2,28,c5,0,0,0,0,0,2,27,43,2,3,40,e8, 64,80,f8,
  //   e9,33,e8,33,60,11,4,60,f0,ed,33,ec,33,70,9,e8,fc,e9,fd,ea,fe,eb,ff,22,4, 60,de,d3,eb,9f,ea,
  //   9e,e9,9d,e8,c2,e7,8c,f0,c2,f7,95,f0,40,c,e8,cc,f8,e9,cd,f9,ea,ce, fa,eb,cf,fb,12,3,b,85,d0,
  //   f0,58,4,70,3,20,d5,b3,e8,4,70,7,50,2,b2,d5,2,3,4a,92,d5, ec,4,60,f7,e4,cc,c0,e0,c3,98,f8,60,
  //   3b,94,18,60,8,40,d,d0,e0,fb,2,3,22,e4,fb,fa,c9, fc,80,28,e8,30,e4,6,e4,c9,fb,e4,ca,fc,e8,30,
  //   e3,5,e4,c9,ca,cb,fc,e8,54,7,60,10,f8, c3,e9,13,f9,ea,13,fa,eb,13,fb,ec,13,fc,d8,f1,30,f5,2f,
  //   c3,e4,9c,fc,ef,9b,ff,ee,9a, fe,ed,99,fd,d0,e0,fb,ef,4e,4d,4c,70,12,22,db,3,2,3,47,ec,2c,fc,
  //   ef,33,ff,ee,33,fe, ed,33,fd,ed,30,e7,eb,2,3,22,ef,2b,ff,ee,3a,fe,ed,39,fd,d0,e0,fb,50,13,b,
  //   bb,0,3,2, 3,4a,ed,13,fd,ee,13,fe,ef,13,ff,ec,13,fc,2,3,22,ec,4d,60,11,e8,49,70,17,ed,33,ec,
  //    33,4,60,d,e4,fc,ff,fe,fd,22,e9,33,e8,33,4,70,f8,2,3,40,12,3,b,58,4,60,9,e4,cc,24, 81,50,6,
  //   28,50,9,2,3,4a,28,40,3,2,3,47,c0,e0,eb,4a,70,44,b9,80,6,d0,e0,fb,2,3,36,ef, 4e,70,1c,bd,80,
  //   8,eb,ff,ea,fe,e9,fd,80,eb,e9,8d,f0,a4,fe,e5,f0,2,1,ff,e9,cd,f9,ea, fe,eb,ff,ef,89,f0,a4,fc,
  //   e5,f0,ce,89,f0,a4,2e,ff,e4,35,f0,cd,89,f0,a4,2d,fe,e4,35, f0,80,67,ef,4e,70,5,bd,80,d7,80,c3,
  //   ef,8b,f0,a4,ac,f0,ee,8b,f0,a4,2c,fc,e4,35,f0,f8, ef,8a,f0,a4,2c,e5,f0,38,fc,e4,33,cb,8d,f0,
  //   a4,2c,fc,e5,f0,3b,f8,ee,8a,f0,a4,2c,fc, e5,f0,38,f8,e4,33,cf,89,f0,a4,2c,fc,e5,f0,38,cf,34,
  //   0,ce,89,f0,a4,2f,ff,e5,f0,3e,fe, e4,33,c9,8d,f0,a4,2e,fe,e5,f0,39,cd,8a,f0,a4,2f,ff,e5,f0,3e,
  //   fe,e4,3d,fd,33,d0,e0, fb,50,7,b,bb,0,f,2,3,4a,ec,2c,fc,ef,33,ff,ee,33,fe,ed,33,fd,2,3,22,2,
  //   3,4a,ec,5d,4, 60,5,e8,59,4,70,3,2,3,40,12,3,b,58,4,60,f6,ec,48,60,f2,ec,70,4,fd,fe,ff,22,c8,
  //   60, db,24,81,c8,50,9,c3,98,60,2,50,6,2,3,47,98,50,ca,f5,82,e9,29,4b,4a,70,5,ab,82,2,3, 36,75,
  //   f0,0,7c,1a,78,80,c3,ef,9b,ee,9a,ed,99,40,d,c3,ef,9b,ff,ee,9a,fe,ed,99,fd,e8, 42,f0,dc,23,ac,
  //   f0,d0,e0,ff,d0,e0,fe,d0,e0,fd,ab,82,20,e7,10,1b,eb,60,ba,ec,2c,fc, ef,33,ff,ee,33,fe,ed,33,
  //   fd,2,3,22,e8,3,f8,30,e7,5,c0,f0,75,f0,0,ef,2f,ff,ee,33,fe, ed,33,fd,40,b8,30,e7,c2,80,aa,ed,
  //   33,ec,33,60,a,4,70,3,bd,80,4,ec,b2,e7,fc,22,75,f0, 20,80,e,75,f0,10,80,5,75,f0,8,7d,0,7e,0,
  //   7f,0,33,92,d5,30,d5,3,12,7,c7,ec,33,40,10, ef,33,ff,ee,33,fe,ed,33,fd,ec,33,fc,d5,f0,ed,22,
  //   e5,f0,24,7e,a2,d5,13,cc,92,e7,cd, ce,ff,22,e9,d2,e7,c9,33,e8,33,f8,92,d5,ed,d2,e7,cd,33,ec,
  //   33,fc,50,2,b2,d5,22,ec,30, e7,10,f,bf,0,c,e,be,0,8,d,bd,0,4,b,eb,60,14,a2,d5,eb,13,fc,ed,92,
  //   e7,fd,22,74,ff,fc, fd,fe,ff,22,e4,80,f8,a2,d5,74,ff,13,fc,7d,80,e4,80,ef,f9,20,e7,36,24,f9,
  //   50,3,79,7, e4,f4,24,2,fb,e5,82,15,82,70,2,15,83,db,f6,e0,24,fb,50,1b,e9,60,14,e4,f0,e5,82,15,
  //    82,70,2,15,83,e0,4,f0,b4,a,8,e4,f0,d9,ee,74,1,f0,a,22,c2,d5,22,ed,33,ec,33,92,d5, fa,60,2a,
  //   b4,ff,33,ed,c2,e7,7b,ff,60,6,7a,3,79,b7,e4,22,7a,3,79,c0,20,d5,4,7a,3,79, bb,22,4e,61,4e,0,
  //   2b,49,4e,46,0,2d,49,4e,46,0,e4,7a,8,f0,a3,da,fc,7b,0,74,7,22,c0, 83,c0,82,ec,c0,e0,ed,c0,e0,
  //   ee,c0,e0,ef,c0,e0,ea,75,f0,10,a4,ca,ab,f0,75,f0,4d,a4, 2b,fb,e4,35,f0,fc,ea,24,10,fa,eb,34,
  //   c5,fb,ec,34,d9,fc,ed,c2,e7,ff,75,f0,56,a4,f4, 24,11,c5,f0,f4,34,c5,8f,f0,a4,2a,e5,f0,3b,e4,
  //   3c,f0,20,e7,14,12,4,c7,d0,e0,ff,d0,e0, fe,d0,e0,fd,d0,e0,fc,12,2,1f,80,14,f4,4,12,4,c7,d0,e0,
  //   ff,d0,e0,fe,d0,e0,fd,d0,e0, fc,12,1,16,d0,82,d0,83,e0,fa,ed,d2,e7,cd,33,ec,33,24,82,fb,e4,c3,
  //   cf,33,cf,ce,33,ce, cd,33,cd,33,db,f3,7b,7,75,f0,a,84,60,4,f0,a3,1b,a,e5,f0,f0,a3,8f,f0,74,a,
  //   a4,ff,ac, f0,8e,f0,74,a,a4,2c,fe,ac,f0,50,1,c,8d,f0,74,a,a4,2c,fd,e4,35,f0,f0,a3,db,de,74,7,
  //    22,3f,80,0,0,41,20,0,0,42,c8,0,0,44,7a,0,0,46,1c,40,0,47,c3,50,0,49,74,24,0,4b,18, 96,80,4c,
  //   be,bc,20,5a,e,1b,ca,67,53,c2,1c,74,9d,c5,ae,fb,60,6,54,7,60,1c,23,23,12, 4,f5,eb,54,38,60,9,
  //   12,4,e1,12,4,f0,12,1,16,ec,f8,ed,f9,ee,fa,ef,cb,22,eb,12,4,f0, 80,f1,54,38,3,24,1c,90,4,97,
  //   fe,93,fc,e,ee,93,fd,e,ee,93,e,ce,93,ff,22,e7,9,f6,8,df, fa,80,46,e7,9,f2,8,df,fa,80,3e,88,82,
  //   8c,83,e7,9,f0,a3,df,fa,80,32,e3,9,f6,8,df,fa, 80,78,e3,9,f2,8,df,fa,80,70,88,82,8c,83,e3,9,
  //   f0,a3,df,fa,80,64,89,82,8a,83,e0,a3, f6,8,df,fa,80,58,89,82,8a,83,e0,a3,f2,8,df,fa,80,4c,80,
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  //   contents of ALUDL (hex, n*v repeats v):
  //   10,21,42,83,4,5,6,7,18,29,4a,8b,c,d,e,f,1,30,53,92,15,14,17,16,9,38,5b,9a,1d,1c,1f, 1e,32,3,
  //   60,a1,26,27,24,25,3a,b,68,a9,2e,2f,2c,2d,23,12,71,b0,37,36,35,34,2b,1a,79, b8,3f,3e,3d,3c,54,
  //   65,6,c7,40,41,42,43,5c,6d,e,cf,48,49,4a,4b,45,74,17,d6,51,50,53, 52,4d,7c,1f,de,59,58,5b,5a,
  //   76,47,24,e5,62,63,60,61,7e,4f,2c,ed,6a,6b,68,69,67,56, 35,f4,73,72,71,70,6f,5e,3d,fc,7b,7a,
  //   79,78,98,a9,ca,b,8c,8d,8e,8f,90,a1,c2,3,84,85, 86,87,89,b8,db,1a,9d,9c,9f,9e,81,b0,d3,12,95,
  //   94,97,96,ba,8b,e8,29,ae,af,ac,ad,b2, 83,e0,21,a6,a7,a4,a5,ab,9a,f9,38,bf,be,bd,bc,a3,92,f1,
  //   30,b7,b6,b5,b4,dc,ed,8e,4f, c8,c9,ca,cb,d4,e5,86,47,c0,c1,c2,c3,cd,fc,9f,5e,d9,d8,db,da,c5,
  //   f4,97,56,d1,d0,d3, d2,fe,cf,ac,6d,ea,eb,e8,e9,f6,c7,a4,65,e2,e3,e0,e1,ef,de,bd,7c,fb,fa,f9,
  //   f8,e7,d6, b5,74,f3,f2,f1,f0,0,1,2,3,4,5,6,7,8,9,80,81,82,83,84,85,0,1,2,3,4,5,6,7,8,9,80,81,
  //    82,83,84,85,0,1,2,3,4,5,6,7,8,9,80,81,82,83,84,85,0,1,2,3,4,5,6,7,8,9,80,81,82,83, 84,85,0,
  //   1,2,3,4,5,6,7,8,9,80,81,82,83,84,85,0,1,2,3,4,5,6,7,8,9,80,81,82,83,84,85, 0,1,2,3,4,5,6,7,
  //   8,9,80,81,82,83,84,85,0,1,2,3,4,5,6,7,8,9,80,81,82,83,84,85,6,7,48, 49,4a,4b,4c,4d,e,f,80,81,
  //   82,83,84,85,6,7,48,49,4a,4b,4c,4d,e,f,80,81,82,83,84,85, 6,7,48,49,4a,4b,4c,4d,e,f,80,81,82,
  //   83,84,85,6,7,48,49,4a,4b,4c,4d,e,f,80,81,82,83, 84,85,6,7,48,49,4a,4b,4c,4d,e,f,80,81,82,83,
  //   84,85,6,7,48,49,4a,4b,4c,4d,e,f,80,81, 82,83,84,85,6,7,48,49,4a,4b,4c,4d,e,f,80,81,82,83,84,
  //   85,6,7,48,49,4a,4b,4c,4d,e,f, 80,81,82,83,84,85,0,1,2,3,4,5,6,7,8,9,a,b,c,d,e,f,1,2,3,4,5,6,
  //   7,48,9,a,b,c,d,e,f, 80,2,3,4,5,6,7,48,49,a,b,c,d,e,f,80,81,3,4,5,6,7,48,49,4a,b,c,d,e,f,80,
  //   81,82,4,5, 6,7,48,49,4a,4b,c,d,e,f,80,81,82,83,5,6,7,48,49,4a,4b,4c,d,e,f,80,81,82,83,84,6,
  //   7, 48,49,4a,4b,4c,4d,e,f,80,81,82,83,84,85,7,48,49,4a,4b,4c,4d,4e,f,80,81,82,83,84,85, 86,8,
  //   9,a,b,c,d,e,f,c0,c1,c2,c3,c4,c5,c6,c7,9,a,b,c,d,e,f,80,c1,c2,c3,c4,c5,c6,c7, 88,a,b,c,d,e,f,
  //   80,81,c2,c3,c4,c5,c6,c7,88,89,b,c,d,e,f,80,81,82,c3,c4,c5,c6,c7,88, 89,8a,c,d,e,f,80,81,82,
  //   83,c4,c5,c6,c7,88,89,8a,8b,d,e,f,80,81,82,83,84,c5,c6,c7,88, 89,8a,8b,8c,e,f,80,81,82,83,84,
  //   85,c6,c7,88,89,8a,8b,8c,8d,f,80,81,82,83,84,85,86, c7,88,89,8a,8b,8c,8d,8e,0,1,2,3,4,5,6,7,
  //   8,9,a,b,c,d,e,f,8f,0,1,2,3,4,5,6,47,8,9,a, b,c,d,e,8e,8f,0,1,2,3,4,5,46,47,8,9,a,b,c,d,8d,8e,
  //   8f,0,1,2,3,4,45,46,47,8,9,a,b,c, 8c,8d,8e,8f,0,1,2,3,44,45,46,47,8,9,a,b,8b,8c,8d,8e,8f,0,1,
  //   2,43,44,45,46,47,8,9,a, 8a,8b,8c,8d,8e,8f,0,1,42,43,44,45,46,47,8,9,89,8a,8b,8c,8d,8e,8f,0,
  //   41,42,43,44,45, 46,47,8,c8,c9,ca,cb,cc,cd,ce,cf,0,1,2,3,4,5,6,7,87,c8,c9,ca,cb,cc,cd,ce,8f,
  //   0,1,2, 3,4,5,6,86,87,c8,c9,ca,cb,cc,cd,8e,8f,0,1,2,3,4,5,85,86,87,c8,c9,ca,cb,cc,8d,8e,8f, 0,
  //   1,2,3,4,84,85,86,87,c8,c9,ca,cb,8c,8d,8e,8f,0,1,2,3,83,84,85,86,87,c8,c9,ca,8b, 8c,8d,8e,8f,
  //   0,1,2,82,83,84,85,86,87,c8,c9,8a,8b,8c,8d,8e,8f,0,1,81,82,83,84,85,86, 87,c8,89,8a,8b,8c,8d,
  //   8e,8f,0,0,81,82,3,84,5,6,87,88,9,a,8b,c,8d,8e,f,0,81,82,3,84, 5,6,87,88,9,a,8b,c,8d,8e,f,0,
  //   81,82,3,84,5,6,87,88,9,a,8b,c,8d,8e,f,0,81,82,3,84,5, 6,87,88,9,a,8b,c,8d,8e,f,0,81,82,3,84,
  //   5,6,87,88,9,a,8b,c,8d,8e,f,0,81,82,3,84,5,6, 87,88,9,a,8b,c,8d,8e,f,0,81,82,3,84,5,6,87,88,
  //   9,a,8b,c,8d,8e,f,0,81,82,3,84,5,6,87, 88,9,a,8b,c,8d,8e,f,0,81,82,3,84,5,6,87,88,9,a,8b,c,8d,
  //   8e,f,0,81,82,3,84,5,6,87,88, 9,a,8b,c,8d,8e,f,0,81,82,3,84,5,6,87,88,9,a,8b,c,8d,8e,f,0,81,
  //   82,3,84,5,6,87,88,9, a,8b,c,8d,8e,f,0,81,82,3,84,5,6,87,88,9,a,8b,c,8d,8e,f,0,81,82,3,84,5,
  //   6,87,88,9,a, 8b,c,8d,8e,f,0,81,82,3,84,5,6,87,88,9,a,8b,c,8d,8e,f,0,81,82,3,84,5,6,87,88,9,
  //   a,8b, c,8d,8e,f,0,11,20,31,40,51,60,71,80,91,a0,b1,c0,d1,e0,f1,10,11,30,31,50,51,70,71, 90,
  //   91,b0,b1,d0,d1,f0,f1,20,31,20,31,60,71,60,71,a0,b1,a0,b1,e0,f1,e0,f1,30,31,30, 31,70,71,70,
  //   71,b0,b1,b0,b1,f0,f1,f0,f1,40,51,60,71,40,51,60,71,c0,d1,e0,f1,c0,d1, e0,f1,50,51,70,71,50,
  //   51,70,71,d0,d1,f0,f1,d0,d1,f0,f1,60,71,60,71,60,71,60,71,e0, f1,e0,f1,e0,f1,e0,f1,70,71,70,
  //   71,70,71,70,71,f0,f1,f0,f1,f0,f1,f0,f1,88,99,a8,b9, c8,d9,e8,f9,88,99,a8,b9,c8,d9,e8,f9,98,
  //   99,b8,b9,d8,d9,f8,f9,98,99,b8,b9,d8,d9,f8, f9,a8,b9,a8,b9,e8,f9,e8,f9,a8,b9,a8,b9,e8,f9,e8,
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  //   contents of ALUS (hex, n*v repeats v):
  //   0,1,2,3,4,5,6,7,40,41,42,43,44,45,46,47,10,11,12,13,14,15,16,17,50,51,52,53,54,55, 56,57,20,
  //   21,22,23,24,25,26,27,60,61,62,63,64,65,66,67,30,31,32,33,34,35,36,37,70, 71,72,73,74,75,76,
  //   77,8,9,a,b,c,d,e,f,48,49,4a,4b,4c,4d,4e,4f,18,19,1a,1b,1c,1d,1e, 1f,58,59,5a,5b,5c,5d,5e,5f,
  //   28,29,2a,2b,2c,2d,2e,2f,68,69,6a,6b,6c,6d,6e,6f,38,39, 3a,3b,3c,3d,3e,3f,78,79,7a,7b,7c,7d,
  //   7e,7f,80,81,82,83,84,85,86,87,c0,c1,c2,c3,c4, c5,c6,c7,90,91,92,93,94,95,96,97,d0,d1,d2,d3,
  //   d4,d5,d6,d7,a0,a1,a2,a3,a4,a5,a6,a7, e0,e1,e2,e3,e4,e5,e6,e7,b0,b1,b2,b3,b4,b5,b6,b7,f0,f1,
  //   f2,f3,f4,f5,f6,f7,88,89,8a, 8b,8c,8d,8e,8f,c8,c9,ca,cb,cc,cd,ce,cf,98,99,9a,9b,9c,9d,9e,9f,
  //   d8,d9,da,db,dc,dd, de,df,a8,a9,aa,ab,ac,ad,ae,af,e8,e9,ea,eb,ec,ed,ee,ef,b8,b9,ba,bb,bc,bd,
  //   be,bf,f8, f9,fa,fb,fc,fd,fe,ff,3,b,13,1b,23,2b,33,3b,3,b,13,1b,23,2b,33,3b,3,b,13,1b,23,2b,
  //    33,3b,3,b,13,1b,23,2b,33,3b,3,b,13,1b,23,2b,33,3b,3,b,13,1b,23,2b,33,3b,3,b,13,1b, 23,2b,33,
  //   3b,3,b,13,1b,23,2b,33,3b,3,b,13,1b,23,2b,33,3b,3,b,13,1b,23,2b,33,3b,3,b, 13,1b,23,2b,33,3b,
  //   3,b,13,1b,23,2b,33,3b,3,b,13,1b,23,2b,33,3b,3,b,13,1b,23,2b,33, 3b,3,b,13,1b,23,2b,33,3b,3,
  //   b,13,1b,23,2b,33,3b,3,b,13,1b,23,2b,33,3b,3,b,13,1b,23, 2b,33,3b,3,b,13,1b,23,2b,33,3b,3,b,
  //   13,1b,23,2b,33,3b,3,b,13,1b,23,2b,33,3b,3,b,13, 1b,23,2b,33,3b,3,b,13,1b,23,2b,33,3b,3,b,13,
  //   1b,23,2b,33,3b,3,b,13,1b,23,2b,33,3b, 3,b,13,1b,23,2b,33,3b,3,b,13,1b,23,2b,33,3b,3,b,13,1b,
  //   23,2b,33,3b,3,b,13,1b,23,2b, 33,3b,3,b,13,1b,23,2b,33,3b,3,b,13,1b,23,2b,33,3b,3,b,13,1b,23,
  //   2b,33,3b,0,1,2,3,4, 5,6,7,8,9,a,b,c,d,e,f,10,11,12,13,14,15,16,17,18,19,1a,1b,1c,1d,1e,1f,20,
  //   21,22,23, 24,25,26,27,28,29,2a,2b,2c,2d,2e,2f,30,31,32,33,34,35,36,37,38,39,3a,3b,3c,3d,3e,
  //    3f,40,41,42,43,44,45,46,47,48,49,4a,4b,4c,4d,4e,4f,50,51,52,53,54,55,56,57,58,59, 5a,5b,5c,
  //   5d,5e,5f,60,61,62,63,64,65,66,67,68,69,6a,6b,6c,6d,6e,6f,70,71,72,73,74, 75,76,77,78,79,7a,
  //   7b,7c,7d,7e,7f,80,81,82,83,84,85,86,87,88,89,8a,8b,8c,8d,8e,8f, 90,91,92,93,94,95,96,97,98,
  //   99,9a,9b,9c,9d,9e,9f,a0,a1,a2,a3,a4,a5,a6,a7,a8,a9,aa, ab,ac,ad,ae,af,b0,b1,b2,b3,b4,b5,b6,
  //   b7,b8,b9,ba,bb,bc,bd,be,bf,c0,c1,c2,c3,c4,c5, c6,c7,c8,c9,ca,cb,cc,cd,ce,cf,d0,d1,d2,d3,d4,
  //   d5,d6,d7,d8,d9,da,db,dc,dd,de,df,e0, e1,e2,e3,e4,e5,e6,e7,e8,e9,ea,eb,ec,ed,ee,ef,f0,f1,f2,
  //   f3,f4,f5,f6,f7,f8,f9,fa,fb, fc,fd,fe,ff,0,0,0,0,0,0,0,0,0,0,0,0,0,0,0,0,0,0,0,0,0,0,0,0,0,0,
  //   0,0,0,0,0,0,0,0,0, 0,0,0,0,0,0,0,0,0,0,0,0,0,0,0,0,0,0,0,0,0,0,0,0,0,0,0,0,0,0,0,0,0,0,0,0,
  //   0,0,0,0,0, 0,0,0,0,0,0,0,0,0,0,0,0,0,0,0,0,0,0,0,0,0,0,0,0,0,0,0,0,0,0,0,0,0,0,0,0,0,0,0,0,
  //   0, 0,0,0,0,0,0,0,0,0,0,0,0,8,9,a,0,0,0,0,0,0,0,0,0,0,0,0,0,0,0,0,0,0,0,0,0,0,0,0,0,0, 0,0,0,
  //   0,0,0,0,0,0,0,b,0,0,0,0,0,0,0,0,0,0,0,0,0,0,0,c,0,0,0,0,0,0,0,0,0,0,0,0,0,0, 0,0,0,0,0,0,0,
  //   0,0,d,0,0,0,0,0,0,0,0,0,0,0,0,0,0,0,e,0,0,0,0,0,0,0,0,0,0,0,0,0,0,0, f,0,0,0,0,0,0,0,0,0,0,
  //   0,0,0,0,0,0,80,1,81,2,82,3,83,4,84,5,85,6,86,7,87,8,88,9,89, a,8a,b,8b,c,8c,d,8d,e,8e,f,8f,
  //   10,90,11,91,12,92,13,93,14,94,15,95,16,96,17,97,18, 98,19,99,1a,9a,1b,9b,1c,9c,1d,9d,1e,9e,
  //   1f,9f,20,a0,21,a1,22,a2,23,a3,24,a4,25,a5, 26,a6,27,a7,28,a8,29,a9,2a,aa,2b,ab,2c,ac,2d,ad,
  //   2e,ae,2f,af,30,b0,31,b1,32,b2,33, b3,34,b4,35,b5,36,b6,37,b7,38,b8,39,b9,3a,ba,3b,bb,3c,bc,
  //   3d,bd,3e,be,3f,bf,40,c0, 41,c1,42,c2,43,c3,44,c4,45,c5,46,c6,47,c7,48,c8,49,c9,4a,ca,4b,cb,
  //   4c,cc,4d,cd,4e, ce,4f,cf,50,d0,51,d1,52,d2,53,d3,54,d4,55,d5,56,d6,57,d7,58,d8,59,d9,5a,da,
  //   5b,db, 5c,dc,5d,dd,5e,de,5f,df,60,e0,61,e1,62,e2,63,e3,64,e4,65,e5,66,e6,67,e7,68,e8,69, e9,
  //   6a,ea,6b,eb,6c,ec,6d,ed,6e,ee,6f,ef,70,f0,71,f1,72,f2,73,f3,74,f4,75,f5,76,f6, 77,f7,78,f8,
  //   79,f9,7a,fa,7b,fb,7c,fc,7d,fd,7e,fe,7f,ff,0,2,4,6,8,a,c,e,10,12,14,16, 18,1a,1c,1e,20,22,24,
  //   26,28,2a,2c,2e,30,32,34,36,38,3a,3c,3e,40,42,44,46,48,4a,4c, 4e,50,52,54,56,58,5a,5c,5e,60,
  //   62,64,66,68,6a,6c,6e,70,72,74,76,78,7a,7c,7e,80,82, 84,86,88,8a,8c,8e,90,92,94,96,98,9a,9c,
  //   9e,a0,a2,a4,a6,a8,aa,ac,ae,b0,b2,b4,b6,b8, ba,bc,be,c0,c2,c4,c6,c8,ca,cc,ce,d0,d2,d4,d6,d8,
  //   da,dc,de,e0,e2,e4,e6,e8,ea,ec,ee, f0,f2,f4,f6,f8,fa,fc,fe,1,3,5,7,9,b,d,f,11,13,15,17,19,1b,
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  //   contents of ALUDH (hex, n*v repeats v):
  //   0,1,2,3,14,25,46,87,8,9,a,b,1c,2d,4e,8f,11,10,13,12,5,34,57,96,19,18,1b,1a,d,3c,5f, 9e,22,23,
  //   20,21,36,7,64,a5,2a,2b,28,29,3e,f,6c,ad,33,32,31,30,27,16,75,b4,3b,3a,39, 38,2f,1e,7d,bc,44,
  //   45,46,47,50,61,2,c3,4c,4d,4e,4f,58,69,a,cb,55,54,57,56,41,70,13, d2,5d,5c,5f,5e,49,78,1b,da,
  //   66,67,64,65,72,43,20,e1,6e,6f,6c,6d,7a,4b,28,e9,77,76, 75,74,63,52,31,f0,7f,7e,7d,7c,6b,5a,
  //   39,f8,88,89,8a,8b,9c,ad,ce,f,80,81,82,83,94,a5, c6,7,99,98,9b,9a,8d,bc,df,1e,91,90,93,92,85,
  //   b4,d7,16,aa,ab,a8,a9,be,8f,ec,2d,a2,a3, a0,a1,b6,87,e4,25,bb,ba,b9,b8,af,9e,fd,3c,b3,b2,b1,
  //   b0,a7,96,f5,34,cc,cd,ce,cf,d8, e9,8a,4b,c4,c5,c6,c7,d0,e1,82,43,dd,dc,df,de,c9,f8,9b,5a,d5,
  //   d4,d7,d6,c1,f0,93,52, ee,ef,ec,ed,fa,cb,a8,69,e6,e7,e4,e5,f2,c3,a0,61,ff,fe,fd,fc,eb,da,b9,
  //   78,f7,f6,f5, f4,e3,d2,b1,70,0,1,2,3,4,5,6,7,8,9,80,81,82,83,84,85,0,1,2,3,4,5,6,7,8,9,80,81,
  //   82, 83,84,85,0,1,2,3,4,5,6,7,8,9,80,81,82,83,84,85,0,1,2,3,4,5,6,7,8,9,80,81,82,83,84, 85,0,
  //   1,2,3,4,5,6,7,8,9,80,81,82,83,84,85,0,1,2,3,4,5,6,7,8,9,80,81,82,83,84,85,0, 1,2,3,4,5,6,7,
  //   8,9,80,81,82,83,84,85,0,1,2,3,4,5,6,7,8,9,80,81,82,83,84,85,6,7,48, 49,4a,4b,4c,4d,e,f,80,81,
  //   82,83,84,85,6,7,48,49,4a,4b,4c,4d,e,f,80,81,82,83,84,85, 6,7,48,49,4a,4b,4c,4d,e,f,80,81,82,
  //   83,84,85,6,7,48,49,4a,4b,4c,4d,e,f,80,81,82,83, 84,85,6,7,48,49,4a,4b,4c,4d,e,f,80,81,82,83,
  //   84,85,6,7,48,49,4a,4b,4c,4d,e,f,80,81, 82,83,84,85,6,7,48,49,4a,4b,4c,4d,e,f,80,81,82,83,84,
  //   85,6,7,48,49,4a,4b,4c,4d,e,f, 80,81,82,83,84,85,0,1,2,3,4,5,6,7,8,9,a,b,c,d,e,f,1,2,3,4,5,6,
  //   7,48,9,a,b,c,d,e,f, 80,2,3,4,5,6,7,48,49,a,b,c,d,e,f,80,81,3,4,5,6,7,48,49,4a,b,c,d,e,f,80,
  //   81,82,4,5, 6,7,48,49,4a,4b,c,d,e,f,80,81,82,83,5,6,7,48,49,4a,4b,4c,d,e,f,80,81,82,83,84,6,
  //   7, 48,49,4a,4b,4c,4d,e,f,80,81,82,83,84,85,7,48,49,4a,4b,4c,4d,4e,f,80,81,82,83,84,85, 86,8,
  //   9,a,b,c,d,e,f,c0,c1,c2,c3,c4,c5,c6,c7,9,a,b,c,d,e,f,80,c1,c2,c3,c4,c5,c6,c7, 88,a,b,c,d,e,f,
  //   80,81,c2,c3,c4,c5,c6,c7,88,89,b,c,d,e,f,80,81,82,c3,c4,c5,c6,c7,88, 89,8a,c,d,e,f,80,81,82,
  //   83,c4,c5,c6,c7,88,89,8a,8b,d,e,f,80,81,82,83,84,c5,c6,c7,88, 89,8a,8b,8c,e,f,80,81,82,83,84,
  //   85,c6,c7,88,89,8a,8b,8c,8d,f,80,81,82,83,84,85,86, c7,88,89,8a,8b,8c,8d,8e,0,1,2,3,4,5,6,7,
  //   8,9,a,b,c,d,e,f,8f,0,1,2,3,4,5,6,47,8,9,a, b,c,d,e,8e,8f,0,1,2,3,4,5,46,47,8,9,a,b,c,d,8d,8e,
  //   8f,0,1,2,3,4,45,46,47,8,9,a,b,c, 8c,8d,8e,8f,0,1,2,3,44,45,46,47,8,9,a,b,8b,8c,8d,8e,8f,0,1,
  //   2,43,44,45,46,47,8,9,a, 8a,8b,8c,8d,8e,8f,0,1,42,43,44,45,46,47,8,9,89,8a,8b,8c,8d,8e,8f,0,
  //   41,42,43,44,45, 46,47,8,c8,c9,ca,cb,cc,cd,ce,cf,0,1,2,3,4,5,6,7,87,c8,c9,ca,cb,cc,cd,ce,8f,
  //   0,1,2, 3,4,5,6,86,87,c8,c9,ca,cb,cc,cd,8e,8f,0,1,2,3,4,5,85,86,87,c8,c9,ca,cb,cc,8d,8e,8f, 0,
  //   1,2,3,4,84,85,86,87,c8,c9,ca,cb,8c,8d,8e,8f,0,1,2,3,83,84,85,86,87,c8,c9,ca,8b, 8c,8d,8e,8f,
  //   0,1,2,82,83,84,85,86,87,c8,c9,8a,8b,8c,8d,8e,8f,0,1,81,82,83,84,85,86, 87,c8,89,8a,8b,8c,8d,
  //   8e,8f,0,0,81,82,3,84,5,6,87,88,9,a,8b,c,8d,8e,f,0,81,82,3,84, 5,6,87,88,9,a,8b,c,8d,8e,f,0,
  //   81,82,3,84,5,6,87,88,9,a,8b,c,8d,8e,f,0,81,82,3,84,5, 6,87,88,9,a,8b,c,8d,8e,f,0,81,82,3,84,
  //   5,6,87,88,9,a,8b,c,8d,8e,f,0,81,82,3,84,5,6, 87,88,9,a,8b,c,8d,8e,f,0,81,82,3,84,5,6,87,88,
  //   9,a,8b,c,8d,8e,f,0,81,82,3,84,5,6,87, 88,9,a,8b,c,8d,8e,f,0,81,82,3,84,5,6,87,88,9,a,8b,c,8d,
  //   8e,f,0,81,82,3,84,5,6,87,88, 9,a,8b,c,8d,8e,f,0,81,82,3,84,5,6,87,88,9,a,8b,c,8d,8e,f,0,81,
  //   82,3,84,5,6,87,88,9, a,8b,c,8d,8e,f,0,81,82,3,84,5,6,87,88,9,a,8b,c,8d,8e,f,0,81,82,3,84,5,
  //   6,87,88,9,a, 8b,c,8d,8e,f,0,81,82,3,84,5,6,87,88,9,a,8b,c,8d,8e,f,0,81,82,3,84,5,6,87,88,9,
  //   a,8b, c,8d,8e,f,0,10,20,30,40,50,60,70,80,90,a0,b0,c0,d0,e0,f0,11,11,31,31,51,51,71,71, 91,
  //   91,b1,b1,d1,d1,f1,f1,20,30,20,30,60,70,60,70,a0,b0,a0,b0,e0,f0,e0,f0,31,31,31, 31,71,71,71,
  //   71,b1,b1,b1,b1,f1,f1,f1,f1,40,50,60,70,40,50,60,70,c0,d0,e0,f0,c0,d0, e0,f0,51,51,71,71,51,
  //   51,71,71,d1,d1,f1,f1,d1,d1,f1,f1,60,70,60,70,60,70,60,70,e0, f0,e0,f0,e0,f0,e0,f0,71,71,71,
  //   71,71,71,71,71,f1,f1,f1,f1,f1,f1,f1,f1,80,90,a0,b0, c0,d0,e0,f0,80,90,a0,b0,c0,d0,e0,f0,91,
  //   91,b1,b1,d1,d1,f1,f1,91,91,b1,b1,d1,d1,f1, f1,a0,b0,a0,b0,e0,f0,e0,f0,a0,b0,a0,b0,e0,f0,e0,
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  //   contents of DECODER (hex, n*v repeats v):
  //   800340152700,95f15854cd00,92f25914cd00,95f15854ce00,92f25914ce00,95f15854c700,92f25914c700,
  //    95f15854c600,92f25914c600,95f15854c500,92f25914c500,95f15854c000,92f25914c000,95f15854bb00,
  //    92f25914bb00,95f15854bb00,92f25914bb00,95f15854b700,92f25914b700,95f15854b700,92f25914b700,
  //    95f15854b700,92f25914b700,95f15854b700,92f25914b700,95f15854b700,92f25914b700,95f15854b700,
  //    92f25914b700,95f15854b700,92f25914b700,95f15854b700,92f25914b700,95f15854a900,92f25914a900,
  //    95f15854d300,92f25914d300,95f158549e00,92f259149e00,95f158549b00,92f259149b00,95f158549a00,
  //    92f259149a00,95f158549400,92f259149400,95f158548f00,92f259148f00,95f158548f00,92f259148f00,
  //    95f158548b00,92f259148b00,95f158548b00,92f259148b00,95f158548b00,92f259148b00,95f158548b00,
  //    92f259148b00,95f158548b00,92f259148b00,95f158548b00,92f259148b00,95f158548b00,92f259148b00,
  //    95f158548b00,92f259148b00,95f158548000,92f259148000,95f15854ce00,92f25914ce00,95f158547b00,
  //    92f259147b00,95f158547a00,92f259147a00,95f158547300,92f259147300,95f158546900,92f259146900,
  //    95f158545f00,92f259145f00,95f158545f00,92f259145f00,95f158545600,92f259145600,95f158545600,
  //    92f259145600,95f158545600,92f259145600,95f158545600,92f259145600,95f158545600,92f259145600,
  //    95f158545600,92f259145600,95f158545600,92f259145600,95f158545600,92f259145600,95f158544b00,
  //    92f259144b00,95f15854d300,92f25914d300,95f158544500,92f259144500,95f158544200,92f259144200,
  //    95f158543a00,92f259143a00,95f158542f00,92f259142f00,95f158542500,92f259142500,95f158542500,
  //    92f259142500,95f158541c00,92f259141c00,95f158541c00,92f259141c00,95f158541c00,92f259141c00,
  //    95f158541c00,92f259141c00,95f158541c00,92f259141c00,95f158541c00,92f259141c00,95f158541c00,
  //    92f259141c00,95f158541c00,92f259141c00,95f158541900,92f259141900,95f15854ce00,92f25914ce00,
  //    95f158541400,92f259141400,95f158540b00,92f259140b00,95f158540900,92f259140900,95f158540500,
  //    92f259140500,95f158540000,92f259140000,95f158540000,92f259140000,95f15853fc00,92f25913fc00,
  //    95f15853fc00,92f25913fc00,95f15853fc00,92f25913fc00,95f15853fc00,92f25913fc00,95f15853fc00,
  //    92f25913fc00,95f15853fc00,92f25913fc00,95f15853fc00,92f25913fc00,95f15853fc00,92f25913fc00,
  //    95f15853f900,92f25913f900,95f15854d300,92f25914d300,95f15853f400,92f25913f400,95f15853eb00,
  //    92f25913eb00,95f15853e900,92f25913e900,95f15853e500,92f25913e500,95f15853e000,92f25913e000,
  //    95f15853e000,92f25913e000,95f15853dc00,92f25913dc00,95f15853dc00,92f25913dc00,95f15853dc00,
  //    92f25913dc00,95f15853dc00,92f25913dc00,95f15853dc00,92f25913dc00,95f15853dc00,92f25913dc00,
  //    95f15853dc00,92f25913dc00,95f15853dc00,92f25913dc00,95f15853d900,92f25913d900,95f15854ce00,
  //    92f25914ce00,95f15853d400,92f25913d400,95f15853cb00,92f25913cb00,95f15853c900,92f25913c900,
  //    95f15853c500,92f25913c500,95f15853c000,92f25913c000,95f15853c000,92f25913c000,95f15853bc00,
  //    92f25913bc00,95f15853bc00,92f25913bc00,95f15853bc00,92f25913bc00,95f15853bc00,92f25913bc00,
  //    95f15853bc00,92f25913bc00,95f15853bc00,92f25913bc00,95f15853bc00,92f25913bc00,95f15853bc00,
  //    92f25913bc00,95f15853b900,92f25913b900,95f15854d300,92f25914d300,95f15853b000,92f25913b000,
  //    95f15853ab00,92f25913ab00,95f15853aa00,92f25913aa00,95f15853a300,92f25913a300,95f158539e00,
  //    92f259139e00,95f158539e00,92f259139e00,95f158539a00,92f259139a00,95f158539a00,92f259139a00,
  //    95f158539a00,92f259139a00,95f158539a00,92f259139a00,95f158539a00,92f259139a00,95f158539a00,
  //    92f259139a00,95f158539a00,92f259139a00,95f158539a00,92f259139a00,95f158539500,92f259139500,
  //    95f15854ce00,92f25914ce00,95f158538c00,92f259138c00,95f158538800,92f259138800,95f158535600,
  //    92f259135600,95f158534c00,92f259134c00,95f158534400,92f259134400,95f158534400,92f259134400,
  //    95f158533d00,92f259133d00,95f158533d00,92f259133d00,95f158533d00,92f259133d00,95f158533d00,
  //    92f259133d00,95f158533d00,92f259133d00,95f158533d00,92f259133d00,95f158533d00,92f259133d00,
  //    95f158533d00,92f259133d00,95f158533900,92f259133900,95f15854d300,92f25914d300,95f158533000,
  //    92f259133000,95f158532c00,92f259132c00,95f158532400,92f259132400,95f158531900,92f259131900,
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endmodule
