// Digital circuit TOP_IAP_test.dig as structural Verilog
module TOP_IAP_test (
  input  CLK,
  input  [11:0] MIPCBI,
  input  MIPCBE,
  input  [15:0] PCBIA1,
  input  PCBE1,
  input  [15:0] PCBIA2,
  input  PCBE2,
  input  [31:0] in_10,
  input  SENTBK,
  input  RECK,
  input  in_14,
  output CLK_2,
  output [7:0] BUS_D,
  output [11:0] MIPC
);

  wire and_1_out, and_3_out, and_4_out, and_5_out, and_6_out, ASSERT_f_to, AST_FAIL, button_1_out,
       button_4_out, button_5_out, comparator_1_eq, comparator_2_eq, comparator_3_eq, comparator_4_eq,
       core_1_p16, dipswitch_1_out, GENCLKBRK, nCLR, nINT1, nIRR_CLR, nITN0, nor_1_out, not_1_out, not_2_out,
       nSFR_OE, nSFR_WE, or_1_out, reset_1_out, sfr_ctl_1_noe, sfr_ctl_2_noe, sfr_ctl_2_nwe, sfr_ctl_3_noe;
  wire [7:0] ADDR_SFR, bitextender_1_out, bitextender_2_out, opcode_q, received_d, sent_d, xor_1_out;
  wire [15:0] PC;
  wire [23:0] counter_1_out, counter_2_out, counter_3_out;
  wire [31:0] add_1_s, add_2_s, add_3_s, op_count_d, op_tick_total_d, op_tickcnt_out, tick_total;

  SFR_CTL sfr_ctl_1 (
    .nSFR_WE(nSFR_WE), .nSFR_OE(nSFR_OE), .A(ADDR_SFR), .MADDR(8'hb0), .nOE(sfr_ctl_1_noe));  // open: nWE
  SFR_CTL sfr_ctl_2 (
    .nSFR_WE(nSFR_WE), .nSFR_OE(nSFR_OE), .A(ADDR_SFR), .MADDR(8'h99), .nWE(sfr_ctl_2_nwe),
    .nOE(sfr_ctl_2_noe));
  ASSERT ASSERT (.C(CLK_2), .A(ADDR_SFR), .D(BUS_D), .nWE(nSFR_WE), .Faf(AST_FAIL), .F_to(ASSERT_f_to));
  BitExtender #(.inputBits(1), .outputBits(8)) bitextender_1 (.in(ASSERT_f_to), .out(bitextender_1_out));
  assign BUS_D = ~sfr_ctl_1_noe ? bitextender_1_out : 8'bz;  // DriverInvSel driverinvsel_1
  Counter #(.Bits(24)) counter_1 (.en(~sfr_ctl_2_nwe), .C(CLK_2), .clr(~nCLR), .out(counter_1_out));  // open: ovf
  Counter #(.Bits(24)) counter_2 (.en(~sfr_ctl_2_noe), .C(CLK_2), .clr(~nCLR), .out(counter_2_out));  // open: ovf
  // Probe on PC
  // Probe on MIPC
  // Probe on counter_1_out
  // Probe on counter_2_out
  not not_1 (not_1_out, sfr_ctl_2_nwe);
  ROM #(.AddrBits(24), .Bits(8)) received (.A(counter_1_out), .sel(1'b1), .D(received_d));
  ROM #(.AddrBits(24), .Bits(8)) sent (.A(counter_2_out), .sel(1'b1), .D(sent_d));
  Button #(.activeLow("true")) button_1 (.out(button_1_out));
  Button #(.activeLow("true")) button_2 (.out(nITN0));
  Button #(.activeLow("true")) button_3 (.out(nINT1));
  Comparator #(.Bits(12)) comparator_1 (.a(MIPCBI), .b(MIPC), .eq(comparator_1_eq));  // open: gt, lt
  Comparator #(.Bits(16)) comparator_2 (.a(PCBIA1), .b(PC), .eq(comparator_2_eq));  // open: gt, lt
  Comparator #(.Bits(16)) comparator_3 (.a(PCBIA2), .b(PC), .eq(comparator_3_eq));  // open: gt, lt
  and and_1 (and_1_out, SENTBK, not_1_out);
  assign xor_1_out = BUS_D ^ received_d;  // XOr xor_1, 8 bits wide
  // Probe on received_d
  // Probe on sent_d
  Reset reset_1 (.out(reset_1_out));
  and and_2 (nCLR, reset_1_out, button_1_out);
  and and_3 (and_3_out, comparator_1_eq, MIPCBE);
  and and_4 (and_4_out, comparator_2_eq, PCBE1);
  and and_5 (and_5_out, comparator_3_eq, PCBE2);
  not not_2 (not_2_out, sfr_ctl_2_noe);
  assign BUS_D = ~sfr_ctl_2_noe ? sent_d : 8'bz;  // DriverInvSel driverinvsel_2
  DipSwitch dipswitch_1 (.out(dipswitch_1_out));
  Comparator #(.Bits(8)) comparator_4 (.a(xor_1_out), .b({8{1'b0}}), .eq(comparator_4_eq));  // open: gt, lt
  and and_6 (and_6_out, RECK, not_2_out);
  Button button_4 (.out(button_4_out));
  Button button_5 (.out(button_5_out));
  or or_1 (or_1_out, and_3_out, and_4_out, and_5_out, GENCLKBRK, and_1_out, nor_1_out, and_6_out);
  nor nor_1 (nor_1_out, sfr_ctl_2_nwe, comparator_4_eq);
  // CORE core_1: pin names not known; wires that end beside it: CLK, nCLR, {8{1'b0}}, button_4_out, dipswitch_1_out, button_5_out, or_1_out, PC, MIPC, CLK_2, BUS_D, ADDR_SFR, nSFR_WE, nSFR_OE, nIRR_CLR, core_1_p16
  Counter #(.Bits(32)) tickcnt (.en(~or_1_out), .C(CLK_2), .clr(~nCLR), .out(tick_total));  // open: ovf
  Comparator #(.Bits(32)) comparator_5 (.a(tick_total), .b(in_10), .eq(GENCLKBRK));  // open: gt, lt
  // Probe tick_total on tick_total
  SFR_CTL sfr_ctl_3 (
    .nSFR_WE(nSFR_WE), .nSFR_OE(nSFR_OE), .A(ADDR_SFR), .MADDR(8'h98), .nOE(sfr_ctl_3_noe));  // open: nWE
  // Probe on BUS_D
  Register #(.Bits(8)) opcode (.D(BUS_D), .C(CLK_2), .en(core_1_p16), .Q(opcode_q));
  Counter #(.Bits(32)) op_tickcnt (.en(1'b1), .C(CLK_2), .clr(core_1_p16), .out(op_tickcnt_out));  // open: ovf
  // Probe on op_tickcnt_out
  BitExtender #(.inputBits(1), .outputBits(8)) bitextender_2 (.in(in_14), .out(bitextender_2_out));
  Counter #(.Bits(24)) counter_3 (.en(core_1_p16), .C(CLK_2), .clr(~nCLR), .out(counter_3_out));  // open: ovf
  Add #(.Bits(32)) add_1 (.a(op_tickcnt_out), .b(32'h1), .c_i(1'b0), .s(add_1_s));  // open: c_o
  assign BUS_D = ~sfr_ctl_3_noe ? bitextender_2_out : 8'bz;  // DriverInvSel driverinvsel_3
  Add #(.Bits(32)) add_2 (.a(add_1_s), .b(op_tick_total_d), .c_i(1'b0), .s(add_2_s));  // open: c_o
  RAMDualPort #(.AddrBits(24), .Bits(16)) PCtrace (
    .A(counter_3_out), .Din(PC), .str(core_1_p16), .C(CLK_2), .ld(1'b1));  // open: D
  RAMDualPort #(.AddrBits(8), .Bits(32)) op_count (
    .A(BUS_D), .Din(add_3_s), .str(core_1_p16), .C(CLK_2), .ld(1'b1), .D(op_count_d));
  // Probe on opcode_q
  Add #(.Bits(32)) add_3 (.a(32'h1), .b(op_count_d), .c_i(1'b0), .s(add_3_s));  // open: c_o
  RAMDualPort #(.AddrBits(8), .Bits(32)) op_tick_total (
    .A(opcode_q), .Din(add_2_s), .str(core_1_p16), .C(CLK_2), .ld(1'b1), .D(op_tick_total_d));
  RAMDualPort #(.AddrBits(8), .Bits(32)) op_tick_aver (
    .A(opcode_q), .Din(add_1_s), .str(core_1_p16), .C(CLK_2), .ld(1'b1));  // open: D

  // Other names for the same wires on the sheet: CLK_t = CLK_2

  // Notes on the sheet:
  //   CLK: Hz: 2147483647
  //   MIPCBI: default 521
  //   PCBIA1: default 65310
  //   in_10: default 4294967295
  //   in_14: default 1
  //   contents of received (hex, n*v repeats v):
  //   0,5a,a5,33,fd,ff,0,1,4,9,10,19,24,31,40,51,64,79,90,a9,c4,e1,0,21,44,69,90,b9,e4,
  //   11,40,71,a4,d9,10,49,84,c1,0,41,84,c9,10,59,a4,f1,40,91,e4,39,90,e9,44,a1,0,61,c4,
  //   29,90,f9,64,d1,40,b1,24,99,10,89,4,81,ff,0,81,4,89,10,99,24,b1,40,d1,64,f9,90,29,
  //   c4,61,0,a1,44,e9,90,39,e4,91,40,f1,a4,59,10,c9,84,41,0,c1,84,49,10,d9,a4,71,40,11,
  //   e4,b9,90,69,44,21,0,e1,c4,a9,90,79,64,51,40,31,24,19,10,9,4,1,0,1,4,9,10,19,24,31,
  //   40,51,64,79,90,a9,c4,e1,0,21,44,69,90,b9,e4,11,40,71,a4,d9,10,49,84,c1,0,41,84,c9,
  //   10,59,a4,f1,40,91,e4,39,90,e9,44,a1,0,61,c4,29,90,f9,64,d1,40,b1,24,99,10,89,4,81,
  //   ff,0,81,4,89,10,99,24,b1,40,d1,64,f9,90,29,c4,61,0,a1,44,e9,90,39,e4,91,40,f1,a4,
  //   59,10,c9,84,41,0,c1,84,49,10,d9,a4,71,40,11,e4,b9,90,69,44,21,0,e1,c4,a9,90,79,64,
  //   51,40,31,24,19,10,9,4,1,0,1,4,9,10,19,24,31,40,51,64,79,90,a9,c4,e1,0,21,44,69,90,
  //   b9,e4,11,40,71,a4,d9,10,49,84,c1,0,41,84,c9,10,59,a4,f1,40,91,e4,39,90,e9,44,a1,0,
  //   61,c4,29,90,f9,64,d1,40,b1,24,99,10,89,4,81,ff,0,81,4,89,10,99,24,b1,40,d1,64,f9,
  //   90,29,c4,61,0,a1,44,e9,90,39,e4,91,40,f1,a4,59,10,c9,84,41,0,c1,84,49,10,d9,a4,71,
  //   40,11,e4,b9,90,69,44,21,0,e1,c4,a9,90,79,64,51,40,31,24,19,10,9,4,1,0,1,4,9,10,19,
  //   24,31,40,51,64,79,90,a9,c4,e1,0,21,44,69,90,b9,e4,11,40,71,a4,d9,10,49,84,c1,0,41,
  //   84,c9,10,59,a4,f1,40,91,e4,39,90,e9,44,a1,0,61,c4,29,90,f9,64,d1,40,b1,24,99,10,89,
  //   4,81,ff,0,81,4,89,10,99,24,b1,40,d1,64,f9,90,29,c4,61,0,a1,44,e9,90,39,e4,91,40,f1,
  //   a4,59,10,c9,84,41,0,c1,84,49,10,d9,a4,71,40,11,e4,b9,90,69,44,21,0,e1,c4,a9,90,79,
  //   64,51,40,31,24,19,10,9,4,1,0,1,4,9,10,19,24,31,40,51,64,79,90,a9,c4,e1,0,21,44,69,
  //   90,b9,e4,11,40,71,a4,d9,10,49,84,c1,0,41,84,c9,10,59,a4,f1,40,91,e4,39,90,e9,44,a1,
  //   0,61,c4,29,90,f9,64,d1,40,b1,24,99,10,89,4,81,ff,0,81,4,89,10,99,24,b1,40,d1,64,f9,
  //   90,29,c4,61,0,a1,44,e9,90,39,e4,91,40,f1,a4,59,10,c9,84,41,0,c1,84,49,10,d9,a4,71,
  //   40,11,e4,b9,90,69,44,21,0,e1,c4,a9,90,79,64,51,40,31,24,19,10,9,4,1,0,1,4,9,10,19,
  //   24,31,40,51,64,79,90,a9,c4,e1,0,21,44,69,90,b9,e4,11,40,71,a4,d9,10,49,84,c1,0,41,
  //   84,c9,10,59,a4,f1,40,91,e4,39,90,e9,44,a1,0,61,c4,29,90,f9,64,d1,40,b1,24,99,10,89,
  //   4,81,ff,0,81,4,89,10,99,24,b1,40,d1,64,f9,90,29,c4,61,0,a1,44,e9,90,39,e4,91,40,f1,
  //   a4,59,10,c9,84,41,0,c1,84,49,10,d9,a4,71,40,11,e4,b9,90,69,44,21,0,e1,c4,a9,90,79,
  //   64,51,40,31,24,19,10,9,4,1,0,1,4,9,10,19,24,31,40,51,64,79,90,a9,c4,e1,0,21,44,69,
  //   90,b9,e4,11,40,71,a4,d9,10,49,84,c1,0,41,84,c9,10,59,a4,f1,40,91,e4,39,90,e9,44,a1,
  //   0,61,c4,29,90,f9,64,d1,40,b1,24,99,10,89,4,81,ff,0,81,4,89,10,99,24,b1,40,d1,64,f9,
  //   90,29,c4,61,0,a1,44,e9,90,39,e4,91,40,f1,a4,59,10,c9,84,41,0,c1,84,49,10,d9,a4,71,
  //   40,11,e4,b9,90,69,44,21,0,e1,c4,a9,90,79,64,51,40,31,24,19,10,9,4,1,0,1,4,9,10,19,
  //   24,31,40,51,64,79,90,a9,c4,e1,0,21,44,69,90,b9,e4,11,40,71,a4,d9,10,49,84,c1,0,41,
  //   84,c9,10,59,a4,f1,40,91,e4,39,90,e9,44,a1,0,61,c4,29,90,f9,64,d1,40,b1,24,99,10,89,
  //   4,81,ff,0,81,4,89,10,99,24,b1,40,d1,64,f9,90,29,c4,61,0,a1,44,e9,90,39,e4,91,40,f1,
  //   a4,59,10,c9,84,41,0,c1,84,49,10,d9,a4,71,40,11,e4,b9,90,69,44,21,0,e1,c4,a9,90,79,
  //   64,51,40,31,24,19,10,9,4,1,0,1,4,9,10,19,24,31,40,51,64,79,90,a9,c4,e1,0,21,44,69,
  //   90,b9,e4,11,40,71,a4,d9,10,49,84,c1,0,41,84,c9,10,59,a4,f1,40,91,e4,39,90,e9,44,a1,
  //   0,61,c4,29,90,f9,64,d1,40,b1,24,99,10,89,4,81,ff,0,81,4,89,10,99,24,b1,40,d1,64,f9,
  //   90,29,c4,61,0,a1,44,e9,90,39,e4,91,40,f1,a4,59,10,c9,84,41,0,c1,84,49,10,d9,a4,71,
  //   40,11,e4,b9,90,69,44,21,0,e1,c4,a9,90,79,64,51,40,31,24,19,10,9,4,1,0,1,4,9,10,19,
  //   24,31,40,51,64,79,90,a9,c4,e1,0,21,44,69,90,b9,e4,11,40,71,a4,d9,10,49,84,c1,0,41,
  //   84,c9,10,59,a4,f1,40,91,e4,39,90,e9,44,a1,0,61,c4,29,90,f9,64,d1,40,b1,24,99,10,89,
  //   4,81,ff,0,81,4,89,10,99,24,b1,40,d1,64,f9,90,29,c4,61,0,a1,44,e9,90,39,e4,91,40,f1,
  //   a4,59,10,c9,84,41,0,c1,84,49,10,d9,a4,71,40,11,e4,b9,90,69,44,21,0,e1,c4,a9,90,79,
  //   64,51,40,31,24,19,10,9,4,1,0,1,4,9,10,19,24,31,40,51,64,79,90,a9,c4,e1,0,21,44,69,
  //   90,b9,e4,11,40,71,a4,d9,10,49,84,c1,0,41,84,c9,10,59,a4,f1,40,91,e4,39,90,e9,44,a1,
  //   0,61,c4,29,90,f9,64,d1,40,b1,24,99,10,89,4,81,ff,0,81,4,89,10,99,24,b1,40,d1,64,f9,
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  //   contents of sent (hex, n*v repeats v):
  //   ff,a5,5a,cc,2,0,40,40,0,0,1,4,9,10,19,24,31,40,51,64,79,90,a9,c4,e1,0,21,44,69,90,
  //   b9,e4,11,40,71,a4,d9,10,49,84,c1,0,41,84,c9,10,59,a4,f1,40,91,e4,39,90,e9,44,a1,0,
  //   61,c4,29,90,f9,64,d1,40,b1,24,99,10,89,4,81,3,40,0,40,0,0,80,80,0,0,81,4,89,10,99,
  //   24,b1,40,d1,64,f9,90,29,c4,61,0,a1,44,e9,90,39,e4,91,40,f1,a4,59,10,c9,84,41,0,c1,
  //   84,49,10,d9,a4,71,40,11,e4,b9,90,69,44,21,0,e1,c4,a9,90,79,64,51,40,31,24,19,10,9,
  //   4,1,0,1,4,9,10,19,24,31,40,51,64,79,90,a9,c4,e1,0,21,44,69,90,b9,e4,11,40,71,a4,d9,
  //   10,49,84,c1,0,41,84,c9,10,59,a4,f1,40,91,e4,39,90,e9,44,a1,0,61,c4,29,90,f9,64,d1,
  //   40,b1,24,99,10,89,4,81,3,80,0,80,0,0,80,0,1,0,81,4,89,10,99,24,b1,40,d1,64,f9,90,
  //   29,c4,61,0,a1,44,e9,90,39,e4,91,40,f1,a4,59,10,c9,84,41,0,c1,84,49,10,d9,a4,71,40,
  //   11,e4,b9,90,69,44,21,0,e1,c4,a9,90,79,64,51,40,31,24,19,10,9,4,1,0,1,4,9,10,19,24,
  //   31,40,51,64,79,90,a9,c4,e1,0,21,44,69,90,b9,e4,11,40,71,a4,d9,10,49,84,c1,0,41,84,
  //   c9,10,59,a4,f1,40,91,e4,39,90,e9,44,a1,0,61,c4,29,90,f9,64,d1,40,b1,24,99,10,89,4,
  //   81,3,0,1,80,0,0,80,80,1,0,81,4,89,10,99,24,b1,40,d1,64,f9,90,29,c4,61,0,a1,44,e9,
  //   90,39,e4,91,40,f1,a4,59,10,c9,84,41,0,c1,84,49,10,d9,a4,71,40,11,e4,b9,90,69,44,21,
  //   0,e1,c4,a9,90,79,64,51,40,31,24,19,10,9,4,1,0,1,4,9,10,19,24,31,40,51,64,79,90,a9,
  //   c4,e1,0,21,44,69,90,b9,e4,11,40,71,a4,d9,10,49,84,c1,0,41,84,c9,10,59,a4,f1,40,91,
  //   e4,39,90,e9,44,a1,0,61,c4,29,90,f9,64,d1,40,b1,24,99,10,89,4,81,3,80,1,80,0,0,80,
  //   0,2,0,81,4,89,10,99,24,b1,40,d1,64,f9,90,29,c4,61,0,a1,44,e9,90,39,e4,91,40,f1,a4,
  //   59,10,c9,84,41,0,c1,84,49,10,d9,a4,71,40,11,e4,b9,90,69,44,21,0,e1,c4,a9,90,79,64,
  //   51,40,31,24,19,10,9,4,1,0,1,4,9,10,19,24,31,40,51,64,79,90,a9,c4,e1,0,21,44,69,90,
  //   b9,e4,11,40,71,a4,d9,10,49,84,c1,0,41,84,c9,10,59,a4,f1,40,91,e4,39,90,e9,44,a1,0,
  //   61,c4,29,90,f9,64,d1,40,b1,24,99,10,89,4,81,3,0,2,80,0,0,80,80,2,0,81,4,89,10,99,
  //   24,b1,40,d1,64,f9,90,29,c4,61,0,a1,44,e9,90,39,e4,91,40,f1,a4,59,10,c9,84,41,0,c1,
  //   84,49,10,d9,a4,71,40,11,e4,b9,90,69,44,21,0,e1,c4,a9,90,79,64,51,40,31,24,19,10,9,
  //   4,1,0,1,4,9,10,19,24,31,40,51,64,79,90,a9,c4,e1,0,21,44,69,90,b9,e4,11,40,71,a4,d9,
  //   10,49,84,c1,0,41,84,c9,10,59,a4,f1,40,91,e4,39,90,e9,44,a1,0,61,c4,29,90,f9,64,d1,
  //   40,b1,24,99,10,89,4,81,3,80,2,80,0,0,80,0,3,0,81,4,89,10,99,24,b1,40,d1,64,f9,90,
  //   29,c4,61,0,a1,44,e9,90,39,e4,91,40,f1,a4,59,10,c9,84,41,0,c1,84,49,10,d9,a4,71,40,
  //   11,e4,b9,90,69,44,21,0,e1,c4,a9,90,79,64,51,40,31,24,19,10,9,4,1,0,1,4,9,10,19,24,
  //   31,40,51,64,79,90,a9,c4,e1,0,21,44,69,90,b9,e4,11,40,71,a4,d9,10,49,84,c1,0,41,84,
  //   c9,10,59,a4,f1,40,91,e4,39,90,e9,44,a1,0,61,c4,29,90,f9,64,d1,40,b1,24,99,10,89,4,
  //   81,3,0,3,80,0,0,80,80,3,0,81,4,89,10,99,24,b1,40,d1,64,f9,90,29,c4,61,0,a1,44,e9,
  //   90,39,e4,91,40,f1,a4,59,10,c9,84,41,0,c1,84,49,10,d9,a4,71,40,11,e4,b9,90,69,44,21,
  //   0,e1,c4,a9,90,79,64,51,40,31,24,19,10,9,4,1,0,1,4,9,10,19,24,31,40,51,64,79,90,a9,
  //   c4,e1,0,21,44,69,90,b9,e4,11,40,71,a4,d9,10,49,84,c1,0,41,84,c9,10,59,a4,f1,40,91,
  //   e4,39,90,e9,44,a1,0,61,c4,29,90,f9,64,d1,40,b1,24,99,10,89,4,81,3,80,3,80,0,0,80,
  //   0,4,0,81,4,89,10,99,24,b1,40,d1,64,f9,90,29,c4,61,0,a1,44,e9,90,39,e4,91,40,f1,a4,
  //   59,10,c9,84,41,0,c1,84,49,10,d9,a4,71,40,11,e4,b9,90,69,44,21,0,e1,c4,a9,90,79,64,
  //   51,40,31,24,19,10,9,4,1,0,1,4,9,10,19,24,31,40,51,64,79,90,a9,c4,e1,0,21,44,69,90,
  //   b9,e4,11,40,71,a4,d9,10,49,84,c1,0,41,84,c9,10,59,a4,f1,40,91,e4,39,90,e9,44,a1,0,
  //   61,c4,29,90,f9,64,d1,40,b1,24,99,10,89,4,81,3,0,4,80,0,0,80,80,4,0,81,4,89,10,99,
  //   24,b1,40,d1,64,f9,90,29,c4,61,0,a1,44,e9,90,39,e4,91,40,f1,a4,59,10,c9,84,41,0,c1,
  //   84,49,10,d9,a4,71,40,11,e4,b9,90,69,44,21,0,e1,c4,a9,90,79,64,51,40,31,24,19,10,9,
  //   4,1,0,1,4,9,10,19,24,31,40,51,64,79,90,a9,c4,e1,0,21,44,69,90,b9,e4,11,40,71,a4,d9,
  //   10,49,84,c1,0,41,84,c9,10,59,a4,f1,40,91,e4,39,90,e9,44,a1,0,61,c4,29,90,f9,64,d1,
  //   40,b1,24,99,10,89,4,81,3,80,4,80,0,0,80,0,5,0,81,4,89,10,99,24,b1,40,d1,64,f9,90,
  //   29,c4,61,0,a1,44,e9,90,39,e4,91,40,f1,a4,59,10,c9,84,41,0,c1,84,49,10,d9,a4,71,40,
  //   11,e4,b9,90,69,44,21,0,e1,c4,a9,90,79,64,51,40,31,24,19,10,9,4,1,0,1,4,9,10,19,24,
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  //   contents of ROM (hex, n*v repeats v):
  //   75,81,7,12,ff,0,75,ff,4,80,fe,7e,ff,7f,ff,80,0,30,b0,5,ad,99,c2,b0,22,ee,4f,60,7, ee,1e,70,
  //   f0,1f,80,ed,22,0,0,0,0,0,0,0,0,0,0,0,0,0,0,0,0,0,0,0,0,0,0,0,0,0,0,0,0,0, 0,0,0,0,0,0,0,0,0,
  //   0,0,0,0,0,0,0,0,0,0,0,0,0,0,0,0,0,0,0,0,0,0,0,0,0,0,0,0,0,0,0,0, 0,0,0,0,0,0,0,0,0,0,0,0,0,
  //   0,0,0,0,0,0,0,0,0,0,0,0,0,0,0,0,0,0,0,0,0,0,0,0,0,0,0,0, 0,0,0,0,0,0,0,0,0,0,0,0,0,0,0,0,0,
  //   0,0,0,0,0,0,0,0,0,0,0,0,0,0,0,0,0,0,0,0,0,0,0,0, 0,0,0,0,0,0,0,0,0,0,0,0,0,0,0,0,0,0,0,0,0,
  //   0,0,0,0,0,0,0,0,0,0,0,0,0,0,0,0,0,0,0,0, 0,0,0,0,0,0,0,0,0,0,0,0,0,0,0,0,0,0,0,0,0,0,0,0,0,
  //   0,0,0,0,0,0,0,0,0,0,0,0,0,0,0,0, 0,0,0,0,0,0,0,0,0,0,0,0,0,0,0,0,0,0,0,0,0,0,0,0,0,0,0,0,0,
  //   0,0,0,0,0,0,0,0,0,0,0,0, 0,0,0,0,0,0,0,0,0,0,0,0,0,0,0,0,0,0,0,0,0,0,0,0,0,0,0,0,0,0,0,0,0,
  //   0,0,0,0,0,0,0,0, 0,0,0,0,0,0,0,0,0,0,0,0,0,0,0,0,0,0,0,0,0,0,0,0,0,0,0,0,0,0,0,0,0,0,0,0,0,
  //   0,0,0,0, 0,0,0,0,0,0,0,0,0,0,0,0,0,0,0,0,0,0,0,0,0,0,0,0,0,0,0,0,0,0,0,0,0,0,0,0,0,0,0,0,0,
  //    0,0,0,0,0,0,0,0,0,0,0,0,0,0,0,0,0,0,0,0,0,0,0,0,0,0,0,0,0,0,0,0,0,0,0,0,0,0,0,0,0, 0,0,0,0,
  //   0,0,0,0,0,0,0,0,0,0,0,0,0,0,0,0,0,0,0,0,0,0,0,0,0,0,0,0,0,0,0,0,0,0,0,0,0, 0,0,0,0,0,0,0,0,
  //   0,0,0,0,0,0,0,0,0,0,0,0,0,0,0,0,0,0,0,0,0,0,0,0,0,0,0,0,0,0,0,0,0, 0,0,0,0,0,0,0,0,0,0,0,0,
  //   0,0,0,0,0,0,0,0,0,0,0,0,0,0,0,0,0,0,0,0,0,0,0,0,0,0,0,0,0, 0,0,0,0,0,0,0,0,0,0,0,0,0,0,0,0,
  //   0,0,0,0,0,0,0,0,0,0,0,0,0,0,0,0,0,0,0,0,0,0,0,0,0, 0,0,0,0,0,0,0,0,0,0,0,0,0,0,0,0,0,0,0,0,
  //   0,0,0,0,0,0,0,0,0,0,0,0,0,0,0,0,0,0,0,0,0, 0,0,0,0,0,0,0,0,0,0,0,0,0,0,0,0,0,0,0,0,0,0,0,0,
  //   0,0,0,0,0,0,0,0,0,0,0,0,0,0,0,0,0, 0,0,0,0,0,0,0,0,0,0,0,0,0,0,0,0,0,0,0,0,0,0,0,0,0,0,0,0,
  //   0,0,0,0,0,0,0,0,0,0,0,0,0, 0,0,0,0,0,0,0,0,0,0,0,0,0,0,0,0,0,0,0,0,0,0,0,0,0,0,0,0,0,0,0,0,
  //   0,0,0,0,0,0,0,0,0, 0,0,0,0,0,0,0,0,0,0,0,0,0,0,0,0,0,0,0,0,0,0,0,0,0,0,0,0,0,0,0,0,0,0,0,0,
  //   0,0,0,0,0, 0,0,0,0,0,0,0,0,0,0,0,0,0,0,0,0,0,0,0,0,0,0,0,0,0,0,0,0,0,0,0,0,0,0,0,0,0,0,0,0,
  //   0, 0,0,0,0,0,0,0,0,0,0,0,0,0,0,0,0,0,0,0,0,0,0,0,0,0,0,0,0,0,0,0,0,0,0,0,0,0,0,0,0,0, 0,0,0,
  //   0,0,0,0,0,0,0,0,0,0,0,0,0,0,0,0,0,0,0,0,0,0,0,0,0,0,0,0,0,0,0,0,0,0,0,0,0,0, 0,0,0,0,0,0,0,
  //   0,0,0,0,0,0,0,0,0,0,0,0,0,0,0,0,0,0,0,0,0,0,0,0,0,0,0,0,0,0,0,0,0,0, 0,0,0,0,0,0,0,0,0,0,0,
  //   0,0,0,0,0,0,0,0,0,0,0,0,0,0,0,0,0,0,0,0,0,0,0,0,0,0,0,0,0,0, 0,0,0,0,0,0,0,0,0,0,0,0,0,0,0,
  //   0,0,0,0,0,0,0,0,0,0,0,0,0,0,0,0,0,0,0,0,0,0,0,0,0,0, 0,0,0,0,0,0,0,0,0,0,0,0,0,0,0,0,0,0,0,
  //   0,0,0,0,0,0,0,0,0,0,0,0,0,0,0,0,0,0,0,0,0,0, 0,0,0,0,0,0,0,0,0,0,0,0,0,0,0,0,0,0,0,0,0,0,0,
  //   0,0,0,0,0,0,0,0,0,0,0,0,0,0,0,0,0,0, 0,0,0,0,0,0,0,0,0,0,0,0,0,0,0,0,0,0,0,0,0,0,0,0,0,0,0,
  //   0,0,0,0,0,0,0,0,0,0,0,0,0,0, 0,0,0,0,0,0,0,0,0,0,0,0,0,0,0,0,0,0,0,0,0,0,0,0,0,0,0,0,0,0,0,
  //   0,0,0,0,0,0,0,0,0,0, 0,0,0,0,0,0,0,0,0,0,0,0,0,0,0,0,0,0,0,0,0,0,0,0,0,0,0,0,0,0,0,0,0,0,0,
  //   0,0,0,0,0,0, 0,0,0,0,0,0,0,0,0,0,0,0,0,0,0,0,0,0,0,0,0,0,0,0,0,0,0,0,0,0,0,0,0,0,0,0,0,0,0,
  //   0,0, 0,0,0,0,0,0,0,0,0,0,0,0,0,0,0,0,0,0,0,0,0,0,0,0,0,0,0,0,0,0,0,0,0,0,0,0,0,0,0,0,0, 0,0,
  //   0,0,0,0,0,0,0,0,0,0,0,0,0,0,0,0,0,0,0,0,0,0,0,0,0,0,0,0,0,0,0,0,0,0,0,0,0,0,0, 0,0,0,0,0,0,
  //   0,0,0,0,0,0,0,0,0,0,0,0,0,0,0,0,0,0,0,0,0,0,0,0,0,0,0,0,0,0,0,0,0,0,0, 0,0,0,0,0,0,0,0,0,0,
  //   0,0,0,0,0,0,0,0,0,0,0,0,0,0,0,0,0,0,0,0,0,0,0,0,0,0,0,0,0,0,0, 0,0,0,0,0,0,0,0,0,0,0,0,0,0,
  //   0,0,0,0,0,0,0,0,0,0,0,0,0,0,0,0,0,0,0,0,0,0,0,0,0,0,0, 0,0,0,0,0,0,0,0,0,0,0,0,0,0,0,0,0,0,
  //   0,0,0,0,0,0,0,0,0,0,0,0,0,0,0,0,0,0,0,0,0,0,0, 0,0,0,0,0,0,0,0,0,0,0,0,0,0,0,0,0,0,0,0,0,0,
  //   0,0,0,0,0,0,0,0,0,0,0,0,0,0,0,0,0,0,0, 0,0,0,0,0,0,0,0,0,0,0,0,0,0,0,0,0,0,0,0,0,0,0,0,0,0,
  //   0,0,0,0,0,0,0,0,0,0,0,0,0,0,0, 0,0,0,0,0,0,0,0,0,0,0,0,0,0,0,0,0,0,0,0,0,0,0,0,0,0,0,0,0,0,
  //   0,0,0,0,0,0,0,0,0,0,0, 0,0,0,0,0,0,0,0,0,0,0,0,0,0,0,0,0,0,0,0,0,0,0,0,0,0,0,0,0,0,0,0,0,0,
  //   0,0,0,0,0,0,0, 0,0,0,0,0,0,0,0,0,0,0,0,0,0,0,0,0,0,0,0,0,0,0,0,0,0,0,0,0,0,0,0,0,0,0,0,0,0,
  //   0,0,0, 0,0,0,0,0,0,0,0,0,0,0,0,0,0,0,0,0,0,0,0,0,0,0,0,0,0,0,0,0,0,0,0,0,0,0,0,0,0,0,0,0, 0,
  //   0,0,0,0,0,0,0,0,0,0,0,0,0,0,0,0,0,0,0,0,0,0,0,0,0,0,0,0,0,0,0,0,0,0,0,0,0,0,0,0, 0,0,0,0,0,
  //   0,0,0,0,0,0,0,0,0,0,0,0,0,0,0,0,0,0,0,0,0,0,0,0,0,0,0,0,0,0,0,0,0,0,0,0, 0,0,0,0,0,0,0,0,0,
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  //   contents of ALUDL (hex, n*v repeats v):
  //   10,21,42,83,4,5,6,7,18,29,4a,8b,c,d,e,f,1,30,53,92,15,14,17,16,9,38,5b,9a,1d,1c,1f, 1e,32,3,
  //   60,a1,26,27,24,25,3a,b,68,a9,2e,2f,2c,2d,23,12,71,b0,37,36,35,34,2b,1a,79, b8,3f,3e,3d,3c,54,
  //   65,6,c7,40,41,42,43,5c,6d,e,cf,48,49,4a,4b,45,74,17,d6,51,50,53, 52,4d,7c,1f,de,59,58,5b,5a,
  //   76,47,24,e5,62,63,60,61,7e,4f,2c,ed,6a,6b,68,69,67,56, 35,f4,73,72,71,70,6f,5e,3d,fc,7b,7a,
  //   79,78,98,a9,ca,b,8c,8d,8e,8f,90,a1,c2,3,84,85, 86,87,89,b8,db,1a,9d,9c,9f,9e,81,b0,d3,12,95,
  //   94,97,96,ba,8b,e8,29,ae,af,ac,ad,b2, 83,e0,21,a6,a7,a4,a5,ab,9a,f9,38,bf,be,bd,bc,a3,92,f1,
  //   30,b7,b6,b5,b4,dc,ed,8e,4f, c8,c9,ca,cb,d4,e5,86,47,c0,c1,c2,c3,cd,fc,9f,5e,d9,d8,db,da,c5,
  //   f4,97,56,d1,d0,d3, d2,fe,cf,ac,6d,ea,eb,e8,e9,f6,c7,a4,65,e2,e3,e0,e1,ef,de,bd,7c,fb,fa,f9,
  //   f8,e7,d6, b5,74,f3,f2,f1,f0,0,1,2,3,4,5,6,7,8,9,80,81,82,83,84,85,0,1,2,3,4,5,6,7,8,9,80,81,
  //    82,83,84,85,0,1,2,3,4,5,6,7,8,9,80,81,82,83,84,85,0,1,2,3,4,5,6,7,8,9,80,81,82,83, 84,85,0,
  //   1,2,3,4,5,6,7,8,9,80,81,82,83,84,85,0,1,2,3,4,5,6,7,8,9,80,81,82,83,84,85, 0,1,2,3,4,5,6,7,
  //   8,9,80,81,82,83,84,85,0,1,2,3,4,5,6,7,8,9,80,81,82,83,84,85,6,7,48, 49,4a,4b,4c,4d,e,f,80,81,
  //   82,83,84,85,6,7,48,49,4a,4b,4c,4d,e,f,80,81,82,83,84,85, 6,7,48,49,4a,4b,4c,4d,e,f,80,81,82,
  //   83,84,85,6,7,48,49,4a,4b,4c,4d,e,f,80,81,82,83, 84,85,6,7,48,49,4a,4b,4c,4d,e,f,80,81,82,83,
  //   84,85,6,7,48,49,4a,4b,4c,4d,e,f,80,81, 82,83,84,85,6,7,48,49,4a,4b,4c,4d,e,f,80,81,82,83,84,
  //   85,6,7,48,49,4a,4b,4c,4d,e,f, 80,81,82,83,84,85,0,1,2,3,4,5,6,7,8,9,a,b,c,d,e,f,1,2,3,4,5,6,
  //   7,48,9,a,b,c,d,e,f, 80,2,3,4,5,6,7,48,49,a,b,c,d,e,f,80,81,3,4,5,6,7,48,49,4a,b,c,d,e,f,80,
  //   81,82,4,5, 6,7,48,49,4a,4b,c,d,e,f,80,81,82,83,5,6,7,48,49,4a,4b,4c,d,e,f,80,81,82,83,84,6,
  //   7, 48,49,4a,4b,4c,4d,e,f,80,81,82,83,84,85,7,48,49,4a,4b,4c,4d,4e,f,80,81,82,83,84,85, 86,8,
  //   9,a,b,c,d,e,f,c0,c1,c2,c3,c4,c5,c6,c7,9,a,b,c,d,e,f,80,c1,c2,c3,c4,c5,c6,c7, 88,a,b,c,d,e,f,
  //   80,81,c2,c3,c4,c5,c6,c7,88,89,b,c,d,e,f,80,81,82,c3,c4,c5,c6,c7,88, 89,8a,c,d,e,f,80,81,82,
  //   83,c4,c5,c6,c7,88,89,8a,8b,d,e,f,80,81,82,83,84,c5,c6,c7,88, 89,8a,8b,8c,e,f,80,81,82,83,84,
  //   85,c6,c7,88,89,8a,8b,8c,8d,f,80,81,82,83,84,85,86, c7,88,89,8a,8b,8c,8d,8e,0,1,2,3,4,5,6,7,
  //   8,9,a,b,c,d,e,f,8f,0,1,2,3,4,5,6,47,8,9,a, b,c,d,e,8e,8f,0,1,2,3,4,5,46,47,8,9,a,b,c,d,8d,8e,
  //   8f,0,1,2,3,4,45,46,47,8,9,a,b,c, 8c,8d,8e,8f,0,1,2,3,44,45,46,47,8,9,a,b,8b,8c,8d,8e,8f,0,1,
  //   2,43,44,45,46,47,8,9,a, 8a,8b,8c,8d,8e,8f,0,1,42,43,44,45,46,47,8,9,89,8a,8b,8c,8d,8e,8f,0,
  //   41,42,43,44,45, 46,47,8,c8,c9,ca,cb,cc,cd,ce,cf,0,1,2,3,4,5,6,7,87,c8,c9,ca,cb,cc,cd,ce,8f,
  //   0,1,2, 3,4,5,6,86,87,c8,c9,ca,cb,cc,cd,8e,8f,0,1,2,3,4,5,85,86,87,c8,c9,ca,cb,cc,8d,8e,8f, 0,
  //   1,2,3,4,84,85,86,87,c8,c9,ca,cb,8c,8d,8e,8f,0,1,2,3,83,84,85,86,87,c8,c9,ca,8b, 8c,8d,8e,8f,
  //   0,1,2,82,83,84,85,86,87,c8,c9,8a,8b,8c,8d,8e,8f,0,1,81,82,83,84,85,86, 87,c8,89,8a,8b,8c,8d,
  //   8e,8f,0,0,81,82,3,84,5,6,87,88,9,a,8b,c,8d,8e,f,0,81,82,3,84, 5,6,87,88,9,a,8b,c,8d,8e,f,0,
  //   81,82,3,84,5,6,87,88,9,a,8b,c,8d,8e,f,0,81,82,3,84,5, 6,87,88,9,a,8b,c,8d,8e,f,0,81,82,3,84,
  //   5,6,87,88,9,a,8b,c,8d,8e,f,0,81,82,3,84,5,6, 87,88,9,a,8b,c,8d,8e,f,0,81,82,3,84,5,6,87,88,
  //   9,a,8b,c,8d,8e,f,0,81,82,3,84,5,6,87, 88,9,a,8b,c,8d,8e,f,0,81,82,3,84,5,6,87,88,9,a,8b,c,8d,
  //   8e,f,0,81,82,3,84,5,6,87,88, 9,a,8b,c,8d,8e,f,0,81,82,3,84,5,6,87,88,9,a,8b,c,8d,8e,f,0,81,
  //   82,3,84,5,6,87,88,9, a,8b,c,8d,8e,f,0,81,82,3,84,5,6,87,88,9,a,8b,c,8d,8e,f,0,81,82,3,84,5,
  //   6,87,88,9,a, 8b,c,8d,8e,f,0,81,82,3,84,5,6,87,88,9,a,8b,c,8d,8e,f,0,81,82,3,84,5,6,87,88,9,
  //   a,8b, c,8d,8e,f,0,11,20,31,40,51,60,71,80,91,a0,b1,c0,d1,e0,f1,10,11,30,31,50,51,70,71, 90,
  //   91,b0,b1,d0,d1,f0,f1,20,31,20,31,60,71,60,71,a0,b1,a0,b1,e0,f1,e0,f1,30,31,30, 31,70,71,70,
  //   71,b0,b1,b0,b1,f0,f1,f0,f1,40,51,60,71,40,51,60,71,c0,d1,e0,f1,c0,d1, e0,f1,50,51,70,71,50,
  //   51,70,71,d0,d1,f0,f1,d0,d1,f0,f1,60,71,60,71,60,71,60,71,e0, f1,e0,f1,e0,f1,e0,f1,70,71,70,
  //   71,70,71,70,71,f0,f1,f0,f1,f0,f1,f0,f1,88,99,a8,b9, c8,d9,e8,f9,88,99,a8,b9,c8,d9,e8,f9,98,
  //   99,b8,b9,d8,d9,f8,f9,98,99,b8,b9,d8,d9,f8, f9,a8,b9,a8,b9,e8,f9,e8,f9,a8,b9,a8,b9,e8,f9,e8,
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  //   contents of ALUS (hex, n*v repeats v):
  //   0,1,2,3,4,5,6,7,40,41,42,43,44,45,46,47,10,11,12,13,14,15,16,17,50,51,52,53,54,55, 56,57,20,
  //   21,22,23,24,25,26,27,60,61,62,63,64,65,66,67,30,31,32,33,34,35,36,37,70, 71,72,73,74,75,76,
  //   77,8,9,a,b,c,d,e,f,48,49,4a,4b,4c,4d,4e,4f,18,19,1a,1b,1c,1d,1e, 1f,58,59,5a,5b,5c,5d,5e,5f,
  //   28,29,2a,2b,2c,2d,2e,2f,68,69,6a,6b,6c,6d,6e,6f,38,39, 3a,3b,3c,3d,3e,3f,78,79,7a,7b,7c,7d,
  //   7e,7f,80,81,82,83,84,85,86,87,c0,c1,c2,c3,c4, c5,c6,c7,90,91,92,93,94,95,96,97,d0,d1,d2,d3,
  //   d4,d5,d6,d7,a0,a1,a2,a3,a4,a5,a6,a7, e0,e1,e2,e3,e4,e5,e6,e7,b0,b1,b2,b3,b4,b5,b6,b7,f0,f1,
  //   f2,f3,f4,f5,f6,f7,88,89,8a, 8b,8c,8d,8e,8f,c8,c9,ca,cb,cc,cd,ce,cf,98,99,9a,9b,9c,9d,9e,9f,
  //   d8,d9,da,db,dc,dd, de,df,a8,a9,aa,ab,ac,ad,ae,af,e8,e9,ea,eb,ec,ed,ee,ef,b8,b9,ba,bb,bc,bd,
  //   be,bf,f8, f9,fa,fb,fc,fd,fe,ff,3,b,13,1b,23,2b,33,3b,3,b,13,1b,23,2b,33,3b,3,b,13,1b,23,2b,
  //    33,3b,3,b,13,1b,23,2b,33,3b,3,b,13,1b,23,2b,33,3b,3,b,13,1b,23,2b,33,3b,3,b,13,1b, 23,2b,33,
  //   3b,3,b,13,1b,23,2b,33,3b,3,b,13,1b,23,2b,33,3b,3,b,13,1b,23,2b,33,3b,3,b, 13,1b,23,2b,33,3b,
  //   3,b,13,1b,23,2b,33,3b,3,b,13,1b,23,2b,33,3b,3,b,13,1b,23,2b,33, 3b,3,b,13,1b,23,2b,33,3b,3,
  //   b,13,1b,23,2b,33,3b,3,b,13,1b,23,2b,33,3b,3,b,13,1b,23, 2b,33,3b,3,b,13,1b,23,2b,33,3b,3,b,
  //   13,1b,23,2b,33,3b,3,b,13,1b,23,2b,33,3b,3,b,13, 1b,23,2b,33,3b,3,b,13,1b,23,2b,33,3b,3,b,13,
  //   1b,23,2b,33,3b,3,b,13,1b,23,2b,33,3b, 3,b,13,1b,23,2b,33,3b,3,b,13,1b,23,2b,33,3b,3,b,13,1b,
  //   23,2b,33,3b,3,b,13,1b,23,2b, 33,3b,3,b,13,1b,23,2b,33,3b,3,b,13,1b,23,2b,33,3b,3,b,13,1b,23,
  //   2b,33,3b,0,1,2,3,4, 5,6,7,8,9,a,b,c,d,e,f,10,11,12,13,14,15,16,17,18,19,1a,1b,1c,1d,1e,1f,20,
  //   21,22,23, 24,25,26,27,28,29,2a,2b,2c,2d,2e,2f,30,31,32,33,34,35,36,37,38,39,3a,3b,3c,3d,3e,
  //    3f,40,41,42,43,44,45,46,47,48,49,4a,4b,4c,4d,4e,4f,50,51,52,53,54,55,56,57,58,59, 5a,5b,5c,
  //   5d,5e,5f,60,61,62,63,64,65,66,67,68,69,6a,6b,6c,6d,6e,6f,70,71,72,73,74, 75,76,77,78,79,7a,
  //   7b,7c,7d,7e,7f,80,81,82,83,84,85,86,87,88,89,8a,8b,8c,8d,8e,8f, 90,91,92,93,94,95,96,97,98,
  //   99,9a,9b,9c,9d,9e,9f,a0,a1,a2,a3,a4,a5,a6,a7,a8,a9,aa, ab,ac,ad,ae,af,b0,b1,b2,b3,b4,b5,b6,
  //   b7,b8,b9,ba,bb,bc,bd,be,bf,c0,c1,c2,c3,c4,c5, c6,c7,c8,c9,ca,cb,cc,cd,ce,cf,d0,d1,d2,d3,d4,
  //   d5,d6,d7,d8,d9,da,db,dc,dd,de,df,e0, e1,e2,e3,e4,e5,e6,e7,e8,e9,ea,eb,ec,ed,ee,ef,f0,f1,f2,
  //   f3,f4,f5,f6,f7,f8,f9,fa,fb, fc,fd,fe,ff,0,0,0,0,0,0,0,0,0,0,0,0,0,0,0,0,0,0,0,0,0,0,0,0,0,0,
  //   0,0,0,0,0,0,0,0,0, 0,0,0,0,0,0,0,0,0,0,0,0,0,0,0,0,0,0,0,0,0,0,0,0,0,0,0,0,0,0,0,0,0,0,0,0,
  //   0,0,0,0,0, 0,0,0,0,0,0,0,0,0,0,0,0,0,0,0,0,0,0,0,0,0,0,0,0,0,0,0,0,0,0,0,0,0,0,0,0,0,0,0,0,
  //   0, 0,0,0,0,0,0,0,0,0,0,0,0,8,9,a,0,0,0,0,0,0,0,0,0,0,0,0,0,0,0,0,0,0,0,0,0,0,0,0,0,0, 0,0,0,
  //   0,0,0,0,0,0,0,b,0,0,0,0,0,0,0,0,0,0,0,0,0,0,0,c,0,0,0,0,0,0,0,0,0,0,0,0,0,0, 0,0,0,0,0,0,0,
  //   0,0,d,0,0,0,0,0,0,0,0,0,0,0,0,0,0,0,e,0,0,0,0,0,0,0,0,0,0,0,0,0,0,0, f,0,0,0,0,0,0,0,0,0,0,
  //   0,0,0,0,0,0,80,1,81,2,82,3,83,4,84,5,85,6,86,7,87,8,88,9,89, a,8a,b,8b,c,8c,d,8d,e,8e,f,8f,
  //   10,90,11,91,12,92,13,93,14,94,15,95,16,96,17,97,18, 98,19,99,1a,9a,1b,9b,1c,9c,1d,9d,1e,9e,
  //   1f,9f,20,a0,21,a1,22,a2,23,a3,24,a4,25,a5, 26,a6,27,a7,28,a8,29,a9,2a,aa,2b,ab,2c,ac,2d,ad,
  //   2e,ae,2f,af,30,b0,31,b1,32,b2,33, b3,34,b4,35,b5,36,b6,37,b7,38,b8,39,b9,3a,ba,3b,bb,3c,bc,
  //   3d,bd,3e,be,3f,bf,40,c0, 41,c1,42,c2,43,c3,44,c4,45,c5,46,c6,47,c7,48,c8,49,c9,4a,ca,4b,cb,
  //   4c,cc,4d,cd,4e, ce,4f,cf,50,d0,51,d1,52,d2,53,d3,54,d4,55,d5,56,d6,57,d7,58,d8,59,d9,5a,da,
  //   5b,db, 5c,dc,5d,dd,5e,de,5f,df,60,e0,61,e1,62,e2,63,e3,64,e4,65,e5,66,e6,67,e7,68,e8,69, e9,
  //   6a,ea,6b,eb,6c,ec,6d,ed,6e,ee,6f,ef,70,f0,71,f1,72,f2,73,f3,74,f4,75,f5,76,f6, 77,f7,78,f8,
  //   79,f9,7a,fa,7b,fb,7c,fc,7d,fd,7e,fe,7f,ff,0,2,4,6,8,a,c,e,10,12,14,16, 18,1a,1c,1e,20,22,24,
  //   26,28,2a,2c,2e,30,32,34,36,38,3a,3c,3e,40,42,44,46,48,4a,4c, 4e,50,52,54,56,58,5a,5c,5e,60,
  //   62,64,66,68,6a,6c,6e,70,72,74,76,78,7a,7c,7e,80,82, 84,86,88,8a,8c,8e,90,92,94,96,98,9a,9c,
  //   9e,a0,a2,a4,a6,a8,aa,ac,ae,b0,b2,b4,b6,b8, ba,bc,be,c0,c2,c4,c6,c8,ca,cc,ce,d0,d2,d4,d6,d8,
  //   da,dc,de,e0,e2,e4,e6,e8,ea,ec,ee, f0,f2,f4,f6,f8,fa,fc,fe,1,3,5,7,9,b,d,f,11,13,15,17,19,1b,
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  //   contents of ALUDH (hex, n*v repeats v):
  //   0,1,2,3,14,25,46,87,8,9,a,b,1c,2d,4e,8f,11,10,13,12,5,34,57,96,19,18,1b,1a,d,3c,5f, 9e,22,23,
  //   20,21,36,7,64,a5,2a,2b,28,29,3e,f,6c,ad,33,32,31,30,27,16,75,b4,3b,3a,39, 38,2f,1e,7d,bc,44,
  //   45,46,47,50,61,2,c3,4c,4d,4e,4f,58,69,a,cb,55,54,57,56,41,70,13, d2,5d,5c,5f,5e,49,78,1b,da,
  //   66,67,64,65,72,43,20,e1,6e,6f,6c,6d,7a,4b,28,e9,77,76, 75,74,63,52,31,f0,7f,7e,7d,7c,6b,5a,
  //   39,f8,88,89,8a,8b,9c,ad,ce,f,80,81,82,83,94,a5, c6,7,99,98,9b,9a,8d,bc,df,1e,91,90,93,92,85,
  //   b4,d7,16,aa,ab,a8,a9,be,8f,ec,2d,a2,a3, a0,a1,b6,87,e4,25,bb,ba,b9,b8,af,9e,fd,3c,b3,b2,b1,
  //   b0,a7,96,f5,34,cc,cd,ce,cf,d8, e9,8a,4b,c4,c5,c6,c7,d0,e1,82,43,dd,dc,df,de,c9,f8,9b,5a,d5,
  //   d4,d7,d6,c1,f0,93,52, ee,ef,ec,ed,fa,cb,a8,69,e6,e7,e4,e5,f2,c3,a0,61,ff,fe,fd,fc,eb,da,b9,
  //   78,f7,f6,f5, f4,e3,d2,b1,70,0,1,2,3,4,5,6,7,8,9,80,81,82,83,84,85,0,1,2,3,4,5,6,7,8,9,80,81,
  //   82, 83,84,85,0,1,2,3,4,5,6,7,8,9,80,81,82,83,84,85,0,1,2,3,4,5,6,7,8,9,80,81,82,83,84, 85,0,
  //   1,2,3,4,5,6,7,8,9,80,81,82,83,84,85,0,1,2,3,4,5,6,7,8,9,80,81,82,83,84,85,0, 1,2,3,4,5,6,7,
  //   8,9,80,81,82,83,84,85,0,1,2,3,4,5,6,7,8,9,80,81,82,83,84,85,6,7,48, 49,4a,4b,4c,4d,e,f,80,81,
  //   82,83,84,85,6,7,48,49,4a,4b,4c,4d,e,f,80,81,82,83,84,85, 6,7,48,49,4a,4b,4c,4d,e,f,80,81,82,
  //   83,84,85,6,7,48,49,4a,4b,4c,4d,e,f,80,81,82,83, 84,85,6,7,48,49,4a,4b,4c,4d,e,f,80,81,82,83,
  //   84,85,6,7,48,49,4a,4b,4c,4d,e,f,80,81, 82,83,84,85,6,7,48,49,4a,4b,4c,4d,e,f,80,81,82,83,84,
  //   85,6,7,48,49,4a,4b,4c,4d,e,f, 80,81,82,83,84,85,0,1,2,3,4,5,6,7,8,9,a,b,c,d,e,f,1,2,3,4,5,6,
  //   7,48,9,a,b,c,d,e,f, 80,2,3,4,5,6,7,48,49,a,b,c,d,e,f,80,81,3,4,5,6,7,48,49,4a,b,c,d,e,f,80,
  //   81,82,4,5, 6,7,48,49,4a,4b,c,d,e,f,80,81,82,83,5,6,7,48,49,4a,4b,4c,d,e,f,80,81,82,83,84,6,
  //   7, 48,49,4a,4b,4c,4d,e,f,80,81,82,83,84,85,7,48,49,4a,4b,4c,4d,4e,f,80,81,82,83,84,85, 86,8,
  //   9,a,b,c,d,e,f,c0,c1,c2,c3,c4,c5,c6,c7,9,a,b,c,d,e,f,80,c1,c2,c3,c4,c5,c6,c7, 88,a,b,c,d,e,f,
  //   80,81,c2,c3,c4,c5,c6,c7,88,89,b,c,d,e,f,80,81,82,c3,c4,c5,c6,c7,88, 89,8a,c,d,e,f,80,81,82,
  //   83,c4,c5,c6,c7,88,89,8a,8b,d,e,f,80,81,82,83,84,c5,c6,c7,88, 89,8a,8b,8c,e,f,80,81,82,83,84,
  //   85,c6,c7,88,89,8a,8b,8c,8d,f,80,81,82,83,84,85,86, c7,88,89,8a,8b,8c,8d,8e,0,1,2,3,4,5,6,7,
  //   8,9,a,b,c,d,e,f,8f,0,1,2,3,4,5,6,47,8,9,a, b,c,d,e,8e,8f,0,1,2,3,4,5,46,47,8,9,a,b,c,d,8d,8e,
  //   8f,0,1,2,3,4,45,46,47,8,9,a,b,c, 8c,8d,8e,8f,0,1,2,3,44,45,46,47,8,9,a,b,8b,8c,8d,8e,8f,0,1,
  //   2,43,44,45,46,47,8,9,a, 8a,8b,8c,8d,8e,8f,0,1,42,43,44,45,46,47,8,9,89,8a,8b,8c,8d,8e,8f,0,
  //   41,42,43,44,45, 46,47,8,c8,c9,ca,cb,cc,cd,ce,cf,0,1,2,3,4,5,6,7,87,c8,c9,ca,cb,cc,cd,ce,8f,
  //   0,1,2, 3,4,5,6,86,87,c8,c9,ca,cb,cc,cd,8e,8f,0,1,2,3,4,5,85,86,87,c8,c9,ca,cb,cc,8d,8e,8f, 0,
  //   1,2,3,4,84,85,86,87,c8,c9,ca,cb,8c,8d,8e,8f,0,1,2,3,83,84,85,86,87,c8,c9,ca,8b, 8c,8d,8e,8f,
  //   0,1,2,82,83,84,85,86,87,c8,c9,8a,8b,8c,8d,8e,8f,0,1,81,82,83,84,85,86, 87,c8,89,8a,8b,8c,8d,
  //   8e,8f,0,0,81,82,3,84,5,6,87,88,9,a,8b,c,8d,8e,f,0,81,82,3,84, 5,6,87,88,9,a,8b,c,8d,8e,f,0,
  //   81,82,3,84,5,6,87,88,9,a,8b,c,8d,8e,f,0,81,82,3,84,5, 6,87,88,9,a,8b,c,8d,8e,f,0,81,82,3,84,
  //   5,6,87,88,9,a,8b,c,8d,8e,f,0,81,82,3,84,5,6, 87,88,9,a,8b,c,8d,8e,f,0,81,82,3,84,5,6,87,88,
  //   9,a,8b,c,8d,8e,f,0,81,82,3,84,5,6,87, 88,9,a,8b,c,8d,8e,f,0,81,82,3,84,5,6,87,88,9,a,8b,c,8d,
  //   8e,f,0,81,82,3,84,5,6,87,88, 9,a,8b,c,8d,8e,f,0,81,82,3,84,5,6,87,88,9,a,8b,c,8d,8e,f,0,81,
  //   82,3,84,5,6,87,88,9, a,8b,c,8d,8e,f,0,81,82,3,84,5,6,87,88,9,a,8b,c,8d,8e,f,0,81,82,3,84,5,
  //   6,87,88,9,a, 8b,c,8d,8e,f,0,81,82,3,84,5,6,87,88,9,a,8b,c,8d,8e,f,0,81,82,3,84,5,6,87,88,9,
  //   a,8b, c,8d,8e,f,0,10,20,30,40,50,60,70,80,90,a0,b0,c0,d0,e0,f0,11,11,31,31,51,51,71,71, 91,
  //   91,b1,b1,d1,d1,f1,f1,20,30,20,30,60,70,60,70,a0,b0,a0,b0,e0,f0,e0,f0,31,31,31, 31,71,71,71,
  //   71,b1,b1,b1,b1,f1,f1,f1,f1,40,50,60,70,40,50,60,70,c0,d0,e0,f0,c0,d0, e0,f0,51,51,71,71,51,
  //   51,71,71,d1,d1,f1,f1,d1,d1,f1,f1,60,70,60,70,60,70,60,70,e0, f0,e0,f0,e0,f0,e0,f0,71,71,71,
  //   71,71,71,71,71,f1,f1,f1,f1,f1,f1,f1,f1,80,90,a0,b0, c0,d0,e0,f0,80,90,a0,b0,c0,d0,e0,f0,91,
  //   91,b1,b1,d1,d1,f1,f1,91,91,b1,b1,d1,d1,f1, f1,a0,b0,a0,b0,e0,f0,e0,f0,a0,b0,a0,b0,e0,f0,e0,
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  //   contents of DECODER (hex, n*v repeats v):
  //   800340157e00,95f158552000,92f259152000,95f158552100,92f259152100,95f158551a00,92f259151a00,
  //    95f158551900,92f259151900,95f158551800,92f259151800,95f158551300,92f259151300,95f158550e00,
  //    92f259150e00,95f158550e00,92f259150e00,95f158550a00,92f259150a00,95f158550a00,92f259150a00,
  //    95f158550a00,92f259150a00,95f158550a00,92f259150a00,95f158550a00,92f259150a00,95f158550a00,
  //    92f259150a00,95f158550a00,92f259150a00,95f158550a00,92f259150a00,95f15854fc00,92f25914fc00,
  //    95f158552600,92f259152600,95f15854f100,92f25914f100,95f15854ee00,92f25914ee00,95f15854ed00,
  //    92f25914ed00,95f15854e700,92f25914e700,95f15854e200,92f25914e200,95f15854e200,92f25914e200,
  //    95f15854de00,92f25914de00,95f15854de00,92f25914de00,95f15854de00,92f25914de00,95f15854de00,
  //    92f25914de00,95f15854de00,92f25914de00,95f15854de00,92f25914de00,95f15854de00,92f25914de00,
  //    95f15854de00,92f25914de00,95f15854d300,92f25914d300,95f158552100,92f259152100,95f15854ce00,
  //    92f25914ce00,95f15854cd00,92f25914cd00,95f15854c600,92f25914c600,95f15854bc00,92f25914bc00,
  //    95f15854b200,92f25914b200,95f15854b200,92f25914b200,95f15854a900,92f25914a900,95f15854a900,
  //    92f25914a900,95f15854a900,92f25914a900,95f15854a900,92f25914a900,95f15854a900,92f25914a900,
  //    95f15854a900,92f25914a900,95f15854a900,92f25914a900,95f15854a900,92f25914a900,95f158549e00,
  //    92f259149e00,95f158552600,92f259152600,95f158549800,92f259149800,95f158549500,92f259149500,
  //    95f158548d00,92f259148d00,95f158548200,92f259148200,95f158547800,92f259147800,95f158547800,
  //    92f259147800,95f158546f00,92f259146f00,95f158546f00,92f259146f00,95f158546f00,92f259146f00,
  //    95f158546f00,92f259146f00,95f158546f00,92f259146f00,95f158546f00,92f259146f00,95f158546f00,
  //    92f259146f00,95f158546f00,92f259146f00,95f158546c00,92f259146c00,95f158552100,92f259152100,
  //    95f158546700,92f259146700,95f158545e00,92f259145e00,95f158545c00,92f259145c00,95f158545800,
  //    92f259145800,95f158545300,92f259145300,95f158545300,92f259145300,95f158544f00,92f259144f00,
  //    95f158544f00,92f259144f00,95f158544f00,92f259144f00,95f158544f00,92f259144f00,95f158544f00,
  //    92f259144f00,95f158544f00,92f259144f00,95f158544f00,92f259144f00,95f158544f00,92f259144f00,
  //    95f158544c00,92f259144c00,95f158552600,92f259152600,95f158544700,92f259144700,95f158543e00,
  //    92f259143e00,95f158543c00,92f259143c00,95f158543800,92f259143800,95f158543300,92f259143300,
  //    95f158543300,92f259143300,95f158542f00,92f259142f00,95f158542f00,92f259142f00,95f158542f00,
  //    92f259142f00,95f158542f00,92f259142f00,95f158542f00,92f259142f00,95f158542f00,92f259142f00,
  //    95f158542f00,92f259142f00,95f158542f00,92f259142f00,95f158542c00,92f259142c00,95f158552100,
  //    92f259152100,95f158542700,92f259142700,95f158541e00,92f259141e00,95f158541c00,92f259141c00,
  //    95f158541800,92f259141800,95f158541300,92f259141300,95f158541300,92f259141300,95f158540f00,
  //    92f259140f00,95f158540f00,92f259140f00,95f158540f00,92f259140f00,95f158540f00,92f259140f00,
  //    95f158540f00,92f259140f00,95f158540f00,92f259140f00,95f158540f00,92f259140f00,95f158540f00,
  //    92f259140f00,95f158540c00,92f259140c00,95f158552600,92f259152600,95f158540300,92f259140300,
  //    95f15853fe00,92f25913fe00,95f15853fd00,92f25913fd00,95f15853f600,92f25913f600,95f15853f100,
  //    92f25913f100,95f15853f100,92f25913f100,95f15853ed00,92f25913ed00,95f15853ed00,92f25913ed00,
  //    95f15853ed00,92f25913ed00,95f15853ed00,92f25913ed00,95f15853ed00,92f25913ed00,95f15853ed00,
  //    92f25913ed00,95f15853ed00,92f25913ed00,95f15853ed00,92f25913ed00,95f15853e800,92f25913e800,
  //    95f158552100,92f259152100,95f15853df00,92f25913df00,95f15853db00,92f25913db00,95f15853a900,
  //    92f25913a900,95f158539f00,92f259139f00,95f158539700,92f259139700,95f158539700,92f259139700,
  //    95f158539000,92f259139000,95f158539000,92f259139000,95f158539000,92f259139000,95f158539000,
  //    92f259139000,95f158539000,92f259139000,95f158539000,92f259139000,95f158539000,92f259139000,
  //    95f158539000,92f259139000,95f158538c00,92f259138c00,95f158552600,92f259152600,95f158538300,
  //    92f259138300,95f158537f00,92f259137f00,95f158537700,92f259137700,95f158536c00,92f259136c00,
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endmodule
