// Digital circuit XRAM.dig as structural Verilog
// stop ouput clock if input S  is high. if go is 1, clock will ouput normally.
module XRAM (
  input  CLKA,
  input  [15:0] A,
  input  WE,
  input  nOE,
  output [7:0] O
);

  wire nand_1_out;

  nand nand_1 (nand_1_out, WE, CLKA);
  RAMSinglePortSel #(.AddrBits(16), .isProgramMemory("true"), .Bits(8)) XRAM (
    .A(A), .CS(~1'b0), .WE(~nand_1_out), .OE(~nOE), .D(O));

  // Notes on the sheet:
  //   CLKA: Asynchronous clock specially prepared for RAM
  //   A: address
endmodule
