// Digital circuit reg, sync clear.dig as structural Verilog
module reg__sync_clear (
  input  [7:0] D,
  input  CLK,
  input  nRST,
  input  nLE,
  output [7:0] Q
);

  CounterPreset #(.Bits(8), .generic("this.Bits = int(args.Bits);")) counterpreset_1 (
    .en(1'b0), .C(CLK), .dir(1'b0), .in(D), .ld(~nLE), .clr(~nRST), .out(Q));  // open: ovf

  // Notes on the sheet:
  //   D: Input pin of the data word to be stored.
  //   CLK: Clock input. A rising edge stores the value at the D pin.
  //   Q: Returns the stored value.
  //   nRST: sync clear pin. Reset value to zero when raise edge at CLK pin and this pin is high, higher priority than LE.
  //   nLE: Enable pin. Storing a value works only if this pin is set low.
endmodule
