// Digital circuit reg-file.dig as structural Verilog
module reg_file (
  input  CLK,
  input  [3:0] RS,
  input  [7:0] D,
  input  LLE,
  input  HLE,
  output [7:0] Q
);

  wire [3:0] multiplexer_1_out, multiplexer_2_out;

  Multiplexer #(.Bits(4)) multiplexer_1 (.sel(LLE), .in_0(Q[3:0]), .in_1(D[3:0]), .out(multiplexer_1_out));
  Multiplexer #(.Bits(4)) multiplexer_2 (.sel(HLE), .in_0(Q[7:4]), .in_1(D[7:4]), .out(multiplexer_2_out));
  RAMDualPort #(.AddrBits(4), .Bits(8)) RFL (
    .A(RS), .Din({multiplexer_2_out, multiplexer_1_out}), .str(1'b1), .C(CLK), .ld(1'b1), .D(Q));
endmodule
